// Logisim project main.circ as structural Verilog
module motherboard (
  input  [15:0] in_1,
  input  [15:0] in_2,
  input  [15:0] in_3
);

  wire clock_1_out, memory_1_clkram, memory_1_writeram;
  wire [1:0] sap_2_cpu_1_ramctrl;
  wire [3:0] binary_to_bcd_converter_1_p2, binary_to_bcd_converter_1_p3, binary_to_bcd_converter_2_p1,
       binary_to_bcd_converter_2_p3, binary_to_bcd_converter_2_p4, binary_to_bcd_converter_2_p5,
       sap_2_cpu_1_device_id_port;
  wire [7:0] memory_1_addrram;
  wire [15:0] demultiplexer_1_out0, memory_1_dataout, memory_1_ramin, multiplexer_1_out, ram_1_dout,
       register_1_q, sap_2_cpu_1_device_out, sap_2_cpu_1_ramdin, sap_2_cpu_1_ramiout;

  Clock clock_1 (.out(clock_1_out));
  Register #(.width(16)) register_1 (
    .D(demultiplexer_1_out0), .en(1'b1), .clk(clock_1_out), .Q(register_1_q));  // open: clr
  Multiplexer #(.select(4), .width(16)) multiplexer_1 (
    .in0(in_3), .in1(in_2), .in2(in_1), .out(multiplexer_1_out), .sel(sap_2_cpu_1_device_id_port));  // open: in3, in4, in5, in6, in7, in8, in9, in10, in11, in12, in13, in14, in15
  Demultiplexer #(.select(4), .width(16)) demultiplexer_1 (
    .out0(demultiplexer_1_out0), .in(sap_2_cpu_1_device_out), .sel(sap_2_cpu_1_device_id_port));  // open: out1, out2, out3, out4, out5, out6, out7, out8, out9, out10, out11, out12, out13, out14, out15
  Hex_Digit_Display hex_digit_display_1 (.value(binary_to_bcd_converter_1_p2));  // open: dp
  // Binary_to_BCD_converter #(.binvalue(8)) binary_to_bcd_converter_1: pin names not known; wires that end beside it: register_1_q[15:8], binary_to_bcd_converter_1_p2, binary_to_bcd_converter_1_p3
  Hex_Digit_Display hex_digit_display_2 (.value(binary_to_bcd_converter_1_p3));  // open: dp
  Hex_Digit_Display hex_digit_display_3 (.value(binary_to_bcd_converter_2_p1));  // open: dp
  Hex_Digit_Display hex_digit_display_4 (.value(binary_to_bcd_converter_2_p3));  // open: dp
  Hex_Digit_Display hex_digit_display_5 (.value(binary_to_bcd_converter_2_p4));  // open: dp
  // Binary_to_BCD_converter #(.binvalue(8)) binary_to_bcd_converter_2: pin names not known; wires that end beside it: binary_to_bcd_converter_2_p1, register_1_q[7:0], binary_to_bcd_converter_2_p3, binary_to_bcd_converter_2_p4, binary_to_bcd_converter_2_p5
  sap_2_cpu sap_2_cpu_1 (
    .clk(clock_1_out), .sequence_controls(3'b001), .device_in(multiplexer_1_out), .ramDOUT(memory_1_dataout),
    .device_out(sap_2_cpu_1_device_out), .ramIOUT(sap_2_cpu_1_ramiout), .ramDIN(sap_2_cpu_1_ramdin),
    .ramCTRL(sap_2_cpu_1_ramctrl), .device_id_port(sap_2_cpu_1_device_id_port));
  Hex_Digit_Display hex_digit_display_6 (.value(binary_to_bcd_converter_2_p5));  // open: dp
  RAM #(.dataWidth(16), .enables("line")) ram_1 (
    .addr(memory_1_addrram), .we(memory_1_writeram), .clk(memory_1_clkram), .din(memory_1_ramin),
    .dout(ram_1_dout));
  memory memory_1 (
    .clkIN(clock_1_out), .contRM(sap_2_cpu_1_ramctrl), .addrIN(sap_2_cpu_1_ramiout), .ramOUT(ram_1_dout),
    .dataIN(sap_2_cpu_1_ramdin), .dataOUT(memory_1_dataout), .ramIN(memory_1_ramin),
    .addrRAM(memory_1_addrram), .writeRAM(memory_1_writeram), .clkRAM(memory_1_clkram));
endmodule

module sap_2_cpu (
  input  clk,
  input  [2:0] sequence_controls,
  input  [15:0] ramDOUT,
  input  [15:0] device_in,
  output [1:0] ramCTRL,
  output [15:0] ramIOUT,
  output [15:0] ramDIN,
  output [15:0] device_out,
  output [3:0] device_id_port
);

  wire con_1_cirin, con_1_cirrt, en_const4;
  wire [1:0] cmar, regin_8_9, regot_8_9;
  wire [2:0] aluopcode, c_pc, cdio, cmdr;
  wire [3:0] regin_0_3, regin_4_7, regot_0_3, regot_4_7;
  wire [7:0] alu_flags;
  wire [15:0] con_1_addrot, instruction_register_1_ictrl;

  con con_1 (
    .flagsIN(alu_flags), .clk(clk), .seq_con(sequence_controls), .dataIR(instruction_register_1_ictrl),
    .aluopcode(aluopcode), .select_y_4(en_const4), .regin_8_9(regin_8_9), .regot_8_9(regot_8_9),
    .addrOT(con_1_addrot), .cmdr(cmdr), .cmar(cmar), .cram(ramCTRL), .regin_0_3(regin_0_3),
    .regin_4_7(regin_4_7), .regot_0_3(regot_0_3), .regot_4_7(regot_4_7), .c_pc(c_pc), .cirIN(con_1_cirin),
    .cirRT(con_1_cirrt), .cdio(cdio));
  instruction_register instruction_register_1 (
    .iBUS(con_1_addrot), .enIN(con_1_cirin), .clk(clk), .reset(con_1_cirrt),
    .iCTRL(instruction_register_1_ictrl));
  block_register_4 block_register_4_1 (
    .reset(c_pc[2]), .regin_4(regin_0_3), .regot_4(regot_0_3), .clk(clk), .regin(con_1_addrot),
    .regout(con_1_addrot));
  block_register_4 block_register_4_2 (
    .reset(c_pc[2]), .regin_4(regin_4_7), .regot_4(regot_4_7), .clk(clk), .regin(con_1_addrot),
    .regout(con_1_addrot));
  reg_right_2 reg_right_2_1 (.datain(con_1_addrot), .pc(c_pc), .clk(clk), .dataout(con_1_addrot));
  block_memory block_memory_1 (
    .clk(clk), .in_3(con_1_addrot), .mar_control(cmar), .mdr_control(cmdr), .ramDOUT(ramDOUT),
    .out_8(con_1_addrot), .ramIOUT(ramIOUT), .ramDIN(ramDIN));
  block_logic block_logic_1 (
    .clk(clk), .regin(regin_8_9), .regot(regot_8_9), .datain(con_1_addrot), .reset(c_pc[2]),
    .aluopcode(aluopcode), .select_y_4(en_const4), .dataot(con_1_addrot), .flags(alu_flags));
  out_reg out_reg_1 (
    .dIN(con_1_addrot), .clk(clk), .enIO({c_pc[2], cdio}), .devIN(device_in), .dOUT(con_1_addrot),
    .devOUT(device_out), .device_id(device_id_port));

  // Other names for the same wires on the sheet: reset = c_pc[2]; cram[1:0] = ramCTRL
endmodule

module program_counter (
  input  cINC,
  input  [15:0] instADDR,
  input  cJUMP,
  input  clk,
  input  reset,
  input  enOUT,
  output [15:0] incOUT
);

  wire adder_1_cout, and_1_out, not_1_out, or_1_out;
  wire [15:0] adder_1_out, pull_resistor_1_node, register_1_q;

  not not_1 (not_1_out, clk);
  Adder #(.width(16)) adder_1 (.a(register_1_q), .b(instADDR), .out(adder_1_out), .cin(1'b1), .cout(adder_1_cout));
  Pull_Resistor pull_resistor_1 (.node(pull_resistor_1_node));
  Multiplexer #(.disabled("Z"), .enable("true"), .width(16)) multiplexer_1 (
    .in0(adder_1_out), .in1(instADDR), .out(pull_resistor_1_node), .sel(cJUMP), .en(and_1_out));
  and and_1 (and_1_out, or_1_out, not_1_out);
  or or_1 (or_1_out, cJUMP, cINC);
  Register #(.trigger("falling"), .width(16)) register_1 (
    .D(pull_resistor_1_node), .en(cINC), .clk(not_1_out), .Q(register_1_q), .clr(reset));
  Hex_Digit_Display hex_digit_display_1 (.value(register_1_q[15:12]));  // open: dp
  Hex_Digit_Display hex_digit_display_2 (.value(register_1_q[11:8]));  // open: dp
  assign incOUT = enOUT ? register_1_q : 16'bz;  // Controlled_Buffer controlled_buffer_1
  Hex_Digit_Display hex_digit_display_3 (.value(register_1_q[7:4]));  // open: dp
  Hex_Digit_Display hex_digit_display_4 (.value(register_1_q[3:0]));  // open: dp
  // also tied to GND on the sheet: adder_1_cout

  // Notes on the sheet:
  //   Chooses either JUMP or INCREMENT
  //   Incrementation: Addition of previous state. Hence the half-adders
endmodule

module arithmetic_logic_unit (
  input  enALU,
  input  [2:0] alu_op,
  input  [15:0] A,
  input  [15:0] B,
  output [15:0] Result,
  output [7:0] status
);

  wire decoder_1_out1, decoder_1_out2, or_1_out;
  wire [3:0] bit_extender_1_out;
  wire [7:0] addsub16_1_cout;
  wire [15:0] addsub16_1_out_6, and_1_out, multiplexer_1_out, not_1_out, or_2_out, xor_1_out;

  assign bit_extender_1_out = {{1{1'b0}}, alu_op};  // Bit_Extender bit_extender_1
  Hex_Digit_Display hex_digit_display_1 (.value(bit_extender_1_out));  // open: dp
  Decoder #(.enable("false"), .select(3)) decoder_1 (
    .out1(decoder_1_out1), .out2(decoder_1_out2), .out3(decoder_1_out2), .sel(alu_op));  // open: out0, out4, out5, out6, out7
  Pull_Resistor pull_resistor_1 (.node(A));
  Pull_Resistor pull_resistor_2 (.node(B));
  or or_1 (or_1_out, decoder_1_out1, decoder_1_out2);
  addsub16 addsub16_1 (
    .a(A), .b(B), .invert(or_1_out), .cin(decoder_1_out2), .cout(addsub16_1_cout[0]),
    .out_6(addsub16_1_out_6), .overflow(addsub16_1_cout[3]), .aux_flag(addsub16_1_cout[1]));  // open: zero_flag
  assign not_1_out = ~A;  // NOT_Gate not_1, 16 bits wide
  assign and_1_out = A & B;  // AND_Gate and_1, 16 bits wide
  assign or_2_out = A | B;  // OR_Gate or_2, 16 bits wide
  assign xor_1_out = A ^ B;  // XOR_Gate xor_1, 16 bits wide
  Hex_Digit_Display hex_digit_display_2 (.value(A[15:12]));  // open: dp
  Hex_Digit_Display hex_digit_display_3 (.value(A[11:8]));  // open: dp
  Hex_Digit_Display hex_digit_display_4 (.value(B[15:12]));  // open: dp
  Hex_Digit_Display hex_digit_display_5 (.value(B[11:8]));  // open: dp
  Hex_Digit_Display hex_digit_display_6 (.value(multiplexer_1_out[15:12]));  // open: dp
  Multiplexer #(.select(3), .width(16)) multiplexer_1 (
    .in0(addsub16_1_out_6), .in1(addsub16_1_out_6), .in2(addsub16_1_out_6), .in3(addsub16_1_out_6),
    .in4(not_1_out), .in5(and_1_out), .in6(or_2_out), .in7(xor_1_out), .out(multiplexer_1_out), .sel(alu_op));
  Hex_Digit_Display hex_digit_display_7 (.value(A[7:4]));  // open: dp
  Hex_Digit_Display hex_digit_display_8 (.value(A[3:0]));  // open: dp
  Hex_Digit_Display hex_digit_display_9 (.value(B[7:4]));  // open: dp
  Hex_Digit_Display hex_digit_display_10 (.value(B[3:0]));  // open: dp
  Hex_Digit_Display hex_digit_display_11 (.value(multiplexer_1_out[11:8]));  // open: dp
  Hex_Digit_Display hex_digit_display_12 (.value(multiplexer_1_out[7:4]));  // open: dp
  Hex_Digit_Display hex_digit_display_13 (.value(multiplexer_1_out[3:0]));  // open: dp
  Pull_Resistor pull_resistor_3 (.node(multiplexer_1_out));
  zero_negative_identify zero_negative_identify_1 (
    .datain(multiplexer_1_out), .zero(addsub16_1_cout[2]), .negative(addsub16_1_cout[4]));
  assign Result = enALU ? multiplexer_1_out : 16'bz;  // Controlled_Buffer controlled_buffer_1
  Hex_Digit_Display hex_digit_display_14 (.value(addsub16_1_cout[7:4]));  // open: dp
  Pull_Resistor pull_resistor_4 (.node(addsub16_1_cout));
  Hex_Digit_Display hex_digit_display_15 (.value(addsub16_1_cout[3:0]));  // open: dp
  assign status = enALU ? addsub16_1_cout : 8'bz;  // Controlled_Buffer controlled_buffer_2
endmodule

module adder_subractor (
  input  [7:0] B,
  input  subtract,
  input  [7:0] A,
  output [7:0] result,
  output faux,
  output cout
);

  wire full_adder_1_cout, full_adder_2_cout, full_adder_3_cout, full_adder_5_cout, full_adder_6_cout,
       full_adder_7_cout, xor_1_out, xor_2_out, xor_3_out, xor_4_out, xor_5_out, xor_6_out, xor_7_out,
       xor_8_out;

  xor xor_1 (xor_1_out, B[7], subtract);
  xor xor_2 (xor_2_out, B[6], subtract);
  xor xor_3 (xor_3_out, B[5], subtract);
  xor xor_4 (xor_4_out, B[4], subtract);
  xor xor_5 (xor_5_out, B[3], subtract);
  xor xor_6 (xor_6_out, B[2], subtract);
  xor xor_7 (xor_7_out, B[1], subtract);
  xor xor_8 (xor_8_out, B[0], subtract);
  full_adder full_adder_1 (.A(A[0]), .B(xor_8_out), .C(subtract), .S(result[0]), .Cout(full_adder_1_cout));
  full_adder full_adder_2 (.A(A[1]), .B(xor_7_out), .C(full_adder_1_cout), .S(result[1]), .Cout(full_adder_2_cout));
  full_adder full_adder_3 (.A(A[2]), .B(xor_6_out), .C(full_adder_2_cout), .S(result[2]), .Cout(full_adder_3_cout));
  full_adder full_adder_4 (.A(A[3]), .B(xor_5_out), .C(full_adder_3_cout), .S(result[3]), .Cout(faux));
  full_adder full_adder_5 (.A(A[4]), .B(xor_4_out), .C(faux), .S(result[4]), .Cout(full_adder_5_cout));
  full_adder full_adder_6 (.A(A[5]), .B(xor_3_out), .C(full_adder_5_cout), .S(result[5]), .Cout(full_adder_6_cout));
  full_adder full_adder_7 (.A(A[6]), .B(xor_2_out), .C(full_adder_6_cout), .S(result[6]), .Cout(full_adder_7_cout));
  full_adder full_adder_8 (.A(A[7]), .B(xor_1_out), .C(full_adder_7_cout), .S(result[7]), .Cout(cout));
endmodule

module full_adder (
  input  A,
  input  B,
  input  C,
  output S,
  output Cout
);

  wire and_1_out, and_2_out, xor_1_out;

  xor xor_1 (xor_1_out, A, B);
  and and_1 (and_1_out, A, B);
  xor xor_2 (S, xor_1_out, C);
  and and_2 (and_2_out, xor_1_out, C);
  or or_1 (Cout, and_2_out, and_1_out);
endmodule

module half_adder (
  input  A,
  input  B,
  output Sum,
  output Cout
);

  xor xor_1 (Sum, A, B);
  and and_1 (Cout, A, B);
endmodule

module accumulator (
  input  [7:0] dINBUS,
  input  load,
  input  clk,
  input  reset,
  input  store,
  output [7:0] dOUTBUS,
  output [7:0] dOUTADDSUB
);

  wire [3:0] binary_to_bcd_converter_1_p2, binary_to_bcd_converter_1_p3, binary_to_bcd_converter_1_p4;
  wire [7:0] controlled_buffer_1_out;

  assign controlled_buffer_1_out = load ? dINBUS : 8'bz;  // Controlled_Buffer controlled_buffer_1
  D_Flip_Flop d_ff_1 (.D(controlled_buffer_1_out[0]), .clk(clk), .Q(dOUTADDSUB[0]), .reset(reset));  // open: Qn, preset
  D_Flip_Flop d_ff_2 (.D(controlled_buffer_1_out[1]), .clk(clk), .Q(dOUTADDSUB[1]), .reset(reset));  // open: Qn, preset
  D_Flip_Flop d_ff_3 (.D(controlled_buffer_1_out[2]), .clk(clk), .Q(dOUTADDSUB[2]), .reset(reset));  // open: Qn, preset
  D_Flip_Flop d_ff_4 (.D(controlled_buffer_1_out[3]), .clk(clk), .Q(dOUTADDSUB[3]), .reset(reset));  // open: Qn, preset
  D_Flip_Flop d_ff_5 (.D(controlled_buffer_1_out[4]), .clk(clk), .Q(dOUTADDSUB[4]), .reset(reset));  // open: Qn, preset
  D_Flip_Flop d_ff_6 (.D(controlled_buffer_1_out[5]), .clk(clk), .Q(dOUTADDSUB[5]), .reset(reset));  // open: Qn, preset
  D_Flip_Flop d_ff_7 (.D(controlled_buffer_1_out[6]), .clk(clk), .Q(dOUTADDSUB[6]), .reset(reset));  // open: Qn, preset
  D_Flip_Flop d_ff_8 (.D(controlled_buffer_1_out[7]), .clk(clk), .Q(dOUTADDSUB[7]), .reset(reset));  // open: Qn, preset
  Hex_Digit_Display hex_digit_display_1 (.value(binary_to_bcd_converter_1_p2));  // open: dp
  // Binary_to_BCD_converter #(.binvalue(8)) binary_to_bcd_converter_1: pin names not known; wires that end beside it: dOUTADDSUB, binary_to_bcd_converter_1_p2, binary_to_bcd_converter_1_p3, binary_to_bcd_converter_1_p4
  assign dOUTBUS = store ? dOUTADDSUB : 8'bz;  // Controlled_Buffer controlled_buffer_2
  Hex_Digit_Display hex_digit_display_2 (.value(binary_to_bcd_converter_1_p3));  // open: dp
  Hex_Digit_Display hex_digit_display_3 (.value(binary_to_bcd_converter_1_p4));  // open: dp

  // Notes on the sheet:
  //   Another big register
  //   Can output to BUS
endmodule

module instruction_register (
  input  [15:0] iBUS,
  input  enIN,
  input  clk,
  input  reset,
  output [15:0] iCTRL
);

  wire [15:0] controlled_buffer_1_out;

  assign controlled_buffer_1_out = enIN ? iBUS : 16'bz;  // Controlled_Buffer controlled_buffer_1
  Register #(.width(16)) register_1 (.D(controlled_buffer_1_out), .en(enIN), .clk(clk), .Q(iCTRL), .clr(reset));
  Hex_Digit_Display hex_digit_display_1 (.value(iCTRL[15:12]));  // open: dp
  Hex_Digit_Display hex_digit_display_2 (.value(iCTRL[11:8]));  // open: dp
  Hex_Digit_Display hex_digit_display_3 (.value(iCTRL[7:4]));  // open: dp
  Hex_Digit_Display hex_digit_display_4 (.value(iCTRL[3:0]));  // open: dp
endmodule

module memory_address_register (
  input  [15:0] dBUS,
  input  enIN,
  input  clk,
  input  reset,
  input  enOUT,
  output [15:0] dRAM
);

  wire [15:0] controlled_buffer_1_out, register_1_q;

  Register #(.width(16)) register_1 (.D(controlled_buffer_1_out), .en(enIN), .clk(clk), .Q(register_1_q), .clr(reset));
  assign controlled_buffer_1_out = enIN ? dBUS : 16'bz;  // Controlled_Buffer controlled_buffer_1
  Hex_Digit_Display hex_digit_display_1 (.value(register_1_q[3:0]));  // open: dp
  assign dRAM = enOUT ? register_1_q : 16'bz;  // Controlled_Buffer controlled_buffer_2
  Hex_Digit_Display hex_digit_display_2 (.value(register_1_q[7:4]));  // open: dp
  Hex_Digit_Display hex_digit_display_3 (.value(register_1_q[11:8]));  // open: dp
  Hex_Digit_Display hex_digit_display_4 (.value(register_1_q[15:12]));  // open: dp

  // Notes on the sheet:
  //   Registers can be thought of parallel stacks of dflip flops
endmodule

module memory_data_register (
  input  [15:0] ramIN,
  input  [15:0] dIN,
  input  enIN,
  input  enRAM,
  input  erOT,
  input  clk,
  input  reset,
  output [15:0] dOUT,
  output [15:0] ramOUT
);

  wire [15:0] pull_resistor_1_node, register_1_q;

  Register #(.width(16)) register_1 (.D(pull_resistor_1_node), .en(enIN), .clk(clk), .Q(register_1_q), .clr(reset));
  Pull_Resistor pull_resistor_1 (.node(pull_resistor_1_node));
  Multiplexer #(.disabled("Z"), .enable("true"), .width(16)) multiplexer_1 (
    .in0(ramIN), .in1(dIN), .out(pull_resistor_1_node), .sel(enRAM), .en(enIN));
  Hex_Digit_Display hex_digit_display_1 (.value(register_1_q[15:12]));  // open: dp
  Hex_Digit_Display hex_digit_display_2 (.value(register_1_q[11:8]));  // open: dp
  Demultiplexer #(.disabled("Z"), .enable("true"), .tristate("true"), .width(16)) demultiplexer_1 (
    .out0(dOUT), .out1(ramOUT), .in(register_1_q), .sel(enRAM), .en(erOT));
  Hex_Digit_Display hex_digit_display_3 (.value(register_1_q[7:4]));  // open: dp
  Hex_Digit_Display hex_digit_display_4 (.value(register_1_q[3:0]));  // open: dp
endmodule

module reg_left (
  input  clk,
  input  [15:0] in_2,
  input  load_1,
  input  reset_1,
  input  store_1,
  input  enable_1,
  input  load_2,
  input  reset_2,
  input  store_2,
  input  enable_2,
  output [15:0] out_11
);

  wire and_1_out, and_2_out, and_3_out, and_4_out, or_1_out, or_2_out, or_3_out;
  wire [15:0] controlled_buffer_1_out, register_1_q;

  and and_1 (and_1_out, load_1, enable_1);
  and and_2 (and_2_out, store_1, enable_1);
  and and_3 (and_3_out, load_2, enable_2);
  and and_4 (and_4_out, store_2, enable_2);
  assign controlled_buffer_1_out = or_1_out ? in_2 : 16'bz;  // Controlled_Buffer controlled_buffer_1
  or or_1 (or_1_out, and_1_out, and_3_out);
  or or_2 (or_2_out, reset_1, reset_2);
  or or_3 (or_3_out, and_2_out, and_4_out);
  Register #(.width(16)) register_1 (
    .D(controlled_buffer_1_out), .en(or_1_out), .clk(clk), .Q(register_1_q), .clr(or_2_out));
  Hex_Digit_Display hex_digit_display_1 (.value(register_1_q[15:12]));  // open: dp
  assign out_11 = or_3_out ? register_1_q : 16'bz;  // Controlled_Buffer controlled_buffer_2
  Hex_Digit_Display hex_digit_display_2 (.value(register_1_q[11:8]));  // open: dp
  Hex_Digit_Display hex_digit_display_3 (.value(register_1_q[7:4]));  // open: dp
  Hex_Digit_Display hex_digit_display_4 (.value(register_1_q[3:0]));  // open: dp
endmodule

module reg_left_mirror (
  input  clk,
  input  [15:0] in_2,
  input  load_1,
  input  reset_1,
  input  store_1,
  input  enable_1,
  input  load_2,
  input  reset_2,
  input  store_2,
  input  enable_2,
  output [15:0] out_11
);

  wire and_1_out, and_2_out, and_3_out, and_4_out, or_1_out, or_2_out, or_3_out;
  wire [15:0] controlled_buffer_1_out, register_1_q;

  and and_1 (and_1_out, load_2, enable_2);
  and and_2 (and_2_out, store_2, enable_2);
  and and_3 (and_3_out, load_1, enable_1);
  and and_4 (and_4_out, store_1, enable_1);
  assign controlled_buffer_1_out = or_1_out ? in_2 : 16'bz;  // Controlled_Buffer controlled_buffer_1
  or or_1 (or_1_out, and_3_out, and_1_out);
  or or_2 (or_2_out, reset_1, reset_2);
  or or_3 (or_3_out, and_4_out, and_2_out);
  Register #(.width(16)) register_1 (
    .D(controlled_buffer_1_out), .en(or_1_out), .clk(clk), .Q(register_1_q), .clr(or_2_out));
  Hex_Digit_Display hex_digit_display_1 (.value(register_1_q[15:12]));  // open: dp
  assign out_11 = or_3_out ? register_1_q : 16'bz;  // Controlled_Buffer controlled_buffer_2
  Hex_Digit_Display hex_digit_display_2 (.value(register_1_q[11:8]));  // open: dp
  Hex_Digit_Display hex_digit_display_3 (.value(register_1_q[7:4]));  // open: dp
  Hex_Digit_Display hex_digit_display_4 (.value(register_1_q[3:0]));  // open: dp
endmodule

module reg_right (
  input  in_1,
  input  [15:0] in_2,
  input  in_3,
  input  load_1,
  input  reset_1,
  input  store_1,
  input  enable_1,
  input  load_2,
  input  reset_2,
  input  store_2,
  input  enable_2,
  output [15:0] out_12
);

  wire and_1_out, and_2_out, and_3_out, and_4_out, or_1_out, or_2_out, or_3_out;
  wire [15:0] controlled_buffer_1_out, register_1_q;

  and and_1 (and_1_out, load_1, enable_1);
  and and_2 (and_2_out, store_1, enable_1);
  and and_3 (and_3_out, load_2, enable_2);
  and and_4 (and_4_out, store_2, enable_2);
  assign controlled_buffer_1_out = or_1_out ? in_2 : 16'bz;  // Controlled_Buffer controlled_buffer_1
  or or_1 (or_1_out, and_1_out, in_3, and_3_out);
  or or_2 (or_2_out, reset_1, reset_2);
  or or_3 (or_3_out, and_2_out, and_4_out);
  Register #(.width(16)) register_1 (
    .D(controlled_buffer_1_out), .en(or_1_out), .clk(in_1), .Q(register_1_q), .clr(or_2_out));
  Hex_Digit_Display hex_digit_display_1 (.value(register_1_q[15:12]));  // open: dp
  assign out_12 = or_3_out ? register_1_q : 16'bz;  // Controlled_Buffer controlled_buffer_2
  Hex_Digit_Display hex_digit_display_2 (.value(register_1_q[11:8]));  // open: dp
  Hex_Digit_Display hex_digit_display_3 (.value(register_1_q[7:4]));  // open: dp
  Hex_Digit_Display hex_digit_display_4 (.value(register_1_q[3:0]));  // open: dp
endmodule

module reg_right_mirror (
  input  clk,
  input  [15:0] in_2,
  input  load_1,
  input  reset_1,
  input  store_1,
  input  enable_1,
  input  load_2,
  input  reset_2,
  input  store_2,
  input  enable_2,
  output [15:0] out_11
);

  wire and_1_out, and_2_out, and_3_out, and_4_out, or_1_out, or_2_out, or_3_out;
  wire [15:0] controlled_buffer_1_out, register_1_q;

  and and_1 (and_1_out, load_1, enable_1);
  and and_2 (and_2_out, store_1, enable_1);
  and and_3 (and_3_out, load_2, enable_2);
  and and_4 (and_4_out, store_2, enable_2);
  assign controlled_buffer_1_out = or_1_out ? in_2 : 16'bz;  // Controlled_Buffer controlled_buffer_1
  or or_1 (or_1_out, and_1_out, and_3_out);
  or or_2 (or_2_out, reset_1, reset_2);
  or or_3 (or_3_out, and_2_out, and_4_out);
  Register #(.width(16)) register_1 (
    .D(controlled_buffer_1_out), .en(or_1_out), .clk(clk), .Q(register_1_q), .clr(or_2_out));
  Pull_Resistor pull_resistor_1 (.node(controlled_buffer_1_out));
  Hex_Digit_Display hex_digit_display_1 (.value(register_1_q[15:12]));  // open: dp
  Hex_Digit_Display hex_digit_display_2 (.value(register_1_q[11:8]));  // open: dp
  assign out_11 = or_3_out ? register_1_q : 16'bz;  // Controlled_Buffer controlled_buffer_2
  Hex_Digit_Display hex_digit_display_3 (.value(register_1_q[7:4]));  // open: dp
  Hex_Digit_Display hex_digit_display_4 (.value(register_1_q[3:0]));  // open: dp
endmodule

module out_reg (
  input  [15:0] dIN,
  input  clk,
  input  [3:0] enIO,
  input  [15:0] devIN,
  output [15:0] devOUT,
  output [15:0] dOUT,
  output [3:0] device_id
);

  wire [15:0] controlled_buffer_3_out, pull_resistor_1_node;

  assign dOUT = enIO[3] ? devIN : 16'bz;  // Controlled_Buffer controlled_buffer_1
  Pull_Resistor pull_resistor_1 (.node(pull_resistor_1_node));
  assign pull_resistor_1_node = enIO[0] ? dIN : 16'bz;  // Controlled_Buffer controlled_buffer_2
  assign controlled_buffer_3_out = enIO[2] ? dIN : 16'bz;  // Controlled_Buffer controlled_buffer_3
  Register #(.width(16)) register_1 (.D(pull_resistor_1_node), .en(1'b1), .clk(clk), .Q(devOUT), .clr(enIO[1]));
  Register #(.width(4)) register_2 (
    .D(controlled_buffer_3_out[3:0]), .en(1'b1), .clk(clk), .Q(device_id), .clr(enIO[1]));
  Pull_Resistor pull_resistor_2 (.node(controlled_buffer_3_out[3:0]));
  Hex_Digit_Display hex_digit_display_1 (.value(devOUT[15:12]));  // open: dp
  Hex_Digit_Display hex_digit_display_2 (.value(device_id));  // open: dp
  Hex_Digit_Display hex_digit_display_3 (.value(devOUT[11:8]));  // open: dp
  Hex_Digit_Display hex_digit_display_4 (.value(devOUT[7:4]));  // open: dp
  Hex_Digit_Display hex_digit_display_5 (.value(devOUT[3:0]));  // open: dp
endmodule

module controller (
  input  [7:0] dataIR,
  input  stepENABLE,
  input  CLK,
  input  reset,
  input  fZero,
  input  fNega,
  output [7:0] cuADDR,
  output [4:0] PC,
  output [2:0] REG_A,
  output [2:0] MAR,
  output [2:0] ALU,
  output [2:0] MDR,
  output [2:0] REG_B,
  output [1:0] RAM,
  output [3:0] IO,
  output [1:0] IR
);

  wire ADD_out, ALU_NAND_out, ALU_XOR_out, and_1_out, and_2_out, buffer_1_out, buffer_2_out, buffer_3_out,
       buffer_4_out, d_ff_1_q, d_ff_2_q, DEV_IN_out, DEV_OUT_out, g_immediate_out, JUMP_IMM_out,
       JUMP_NEGA_out, JUMP_out, JUMP_ZERO_out, LOAD_A_IMM_out, LOAD_A_out, LOAD_B_out, not_1_out, not_2_out,
       not_3_out, not_4_out, sequencer_1_execute_cycle_1, sequencer_1_execute_cycle_2,
       sequencer_1_execute_cycle_3, sequencer_1_fetch_set_pc, STORE_A_IMM_out, STORE_A_out, SUB_out,
       t4_alu_1_out_2, t4_alu_2_out_2, t4_device_id_out_2, t4_en_mar_in_out, t4_en_pc_out,
       t4_enable_alu_out_2, t4_enable_alu_out_out, t4_immediate_out, t4_jump_pc_out_2, t4_jump_pc_out_out,
       t4_load_reg_a_out_2, t4_mdr_in_out, t4_ram_load_out, t5_en_mdr_out_out_out, t5_immediate_out,
       t5_load_a_out, t5_load_b_out_2, t5_mdr_out_out, t5_ram_store_out_2, t6_enable_alu_out_2,
       t6_enable_alu_out_out, t6_jump_pc_out_2, t6_jump_pc_out_out, undriven;

  or or_1 (IO[3], reset, undriven);
  D_Flip_Flop d_ff_1 (.D(fZero), .clk(CLK), .Q(d_ff_1_q), .reset(IO[3]));  // open: Qn, preset
  D_Flip_Flop d_ff_2 (.D(fNega), .clk(CLK), .Q(d_ff_2_q), .reset(IO[3]));  // open: Qn, preset
  buf buffer_1 (buffer_1_out, dataIR[7]);
  not not_1 (not_1_out, dataIR[7]);
  buf buffer_2 (buffer_2_out, dataIR[6]);
  not not_2 (not_2_out, dataIR[6]);
  buf buffer_3 (buffer_3_out, dataIR[5]);
  not not_3 (not_3_out, dataIR[5]);
  buf buffer_4 (buffer_4_out, dataIR[4]);
  not not_4 (not_4_out, dataIR[4]);
  sequencer sequencer_1 (
    .enSEQ(CLK), .stepCLK(reset), .CLK(stepENABLE), .fetch_set_pc(sequencer_1_fetch_set_pc),
    .fetch_cpy_inst(PC[1]), .fetch_set_ir(IR[0]), .execute_cycle_1(sequencer_1_execute_cycle_1),
    .execute_cycle_2(sequencer_1_execute_cycle_2), .execute_cycle_3(sequencer_1_execute_cycle_3));  // open: op_in, reset, control_decoder_en, decode, halt_out
  and LOAD_A (LOAD_A_out, not_1_out, not_2_out, not_3_out, buffer_4_out);
  and LOAD_A_IMM (LOAD_A_IMM_out, not_1_out, not_2_out, buffer_3_out, not_4_out);
  and LOAD_B (LOAD_B_out, not_1_out, not_2_out, buffer_3_out, buffer_4_out);
  and STORE_A (STORE_A_out, not_1_out, buffer_2_out, buffer_3_out, not_4_out);
  and STORE_A_IMM (STORE_A_IMM_out, not_1_out, buffer_2_out, buffer_3_out, buffer_4_out);
  and DEV_IN (DEV_IN_out, not_1_out, buffer_2_out, not_3_out, not_4_out);
  and DEV_OUT (DEV_OUT_out, not_1_out, buffer_2_out, not_3_out, buffer_4_out);
  and ADD (ADD_out, buffer_1_out, not_2_out, not_3_out, not_4_out);
  and SUB (SUB_out, buffer_1_out, not_2_out, not_3_out, buffer_4_out);
  and ALU_NAND (ALU_NAND_out, buffer_1_out, not_2_out, buffer_3_out, not_4_out);
  and ALU_XOR (ALU_XOR_out, buffer_1_out, not_2_out, buffer_3_out, buffer_4_out);
  and JUMP (JUMP_out, buffer_1_out, buffer_2_out, not_3_out, not_4_out);
  and JUMP_IMM (JUMP_IMM_out, buffer_1_out, buffer_2_out, not_3_out, buffer_4_out);
  and JUMP_ZERO (JUMP_ZERO_out, buffer_1_out, buffer_2_out, buffer_3_out, not_4_out);
  and JUMP_NEGA (JUMP_NEGA_out, buffer_1_out, buffer_2_out, buffer_3_out, buffer_4_out);
  and and_1 (and_1_out, JUMP_ZERO_out, d_ff_1_q);
  and and_2 (and_2_out, JUMP_NEGA_out, d_ff_2_q);
  assign cuADDR = g_immediate_out ? {4'b0000, dataIR[3:0]} : 8'bz;  // Controlled_Buffer controlled_buffer_1
  or t4_immediate (t4_immediate_out, LOAD_B_out, STORE_A_IMM_out, DEV_OUT_out, DEV_IN_out);
  or t4_mdr_in (t4_mdr_in_out, LOAD_A_IMM_out, LOAD_B_out, LOAD_A_out);
  or t4_en_mar_in (t4_en_mar_in_out, LOAD_A_IMM_out, LOAD_B_out, STORE_A_out, STORE_A_IMM_out, LOAD_A_out);
  or t4_ram_load (t4_ram_load_out, LOAD_A_IMM_out, LOAD_B_out, STORE_A_out);
  or t5_mdr_out (t5_mdr_out_out, LOAD_A_out, LOAD_A_IMM_out, LOAD_B_out);
  or t5_load_a (t5_load_a_out, LOAD_A_IMM_out, LOAD_A_out);
  or t5_ram_store (t5_ram_store_out_2, STORE_A_out, STORE_A_IMM_out);
  or t4_device_id (t4_device_id_out_2, DEV_IN_out, DEV_OUT_out);
  or t4_load_reg_a (t4_load_reg_a_out_2, LOAD_A_out, DEV_IN_out, DEV_OUT_out, ADD_out, SUB_out, ALU_NAND_out, ALU_XOR_out, JUMP_out);
  or t4_enable_alu (t4_enable_alu_out_2, ADD_out, SUB_out, ALU_NAND_out, ALU_XOR_out);
  or t4_alu_1 (t4_alu_1_out_2, SUB_out, ALU_XOR_out);
  or t4_alu_2 (t4_alu_2_out_2, ALU_NAND_out, ALU_XOR_out);
  or t5_load_b (t5_load_b_out_2, JUMP_out, JUMP_IMM_out, JUMP_ZERO_out, JUMP_NEGA_out);
  or t6_enable_alu (t6_enable_alu_out_2, JUMP_IMM_out, JUMP_ZERO_out, JUMP_NEGA_out);
  or t4_en_pc (t4_en_pc_out, JUMP_IMM_out, JUMP_ZERO_out, JUMP_NEGA_out);
  or t6_jump_pc (t6_jump_pc_out_2, JUMP_IMM_out, and_1_out, and_2_out);
  or t5_immediate (t5_immediate_out, JUMP_NEGA_out, JUMP_ZERO_out, JUMP_IMM_out);
  and t4_device_id_out (IO[2], t4_device_id_out_2, sequencer_1_execute_cycle_1);
  and t4_load_reg_a_out (REG_A[1], t4_load_reg_a_out_2, sequencer_1_execute_cycle_1);
  and t4_enable_alu_out (t4_enable_alu_out_out, t4_enable_alu_out_2, sequencer_1_execute_cycle_1);
  and t4_alu_1_out (ALU[1], t4_alu_1_out_2, sequencer_1_execute_cycle_1);
  and t4_alu_2_out (ALU[2], t4_alu_2_out_2, sequencer_1_execute_cycle_1);
  and t4_jump_pc (t4_jump_pc_out_2, JUMP_out, sequencer_1_execute_cycle_1);
  and t4_jump_pc_out (t4_jump_pc_out_out, t4_en_pc_out, sequencer_1_execute_cycle_1);
  and t5_en_mdr_out_out (t5_en_mdr_out_out_out, t5_mdr_out_out, sequencer_1_execute_cycle_2);
  and t5_store_reg_a_out (REG_A[0], t5_load_a_out, sequencer_1_execute_cycle_2);
  and t5_store_reg_b_out (REG_B[0], LOAD_B_out, sequencer_1_execute_cycle_2);
  and t5_ram_store_out (RAM[0], t5_ram_store_out_2, sequencer_1_execute_cycle_2);
  and t5_dev_in (IO[0], DEV_IN_out, sequencer_1_execute_cycle_2);
  and t5_dev_out (IO[1], DEV_OUT_out, sequencer_1_execute_cycle_2);
  and t5_load_b_out (REG_B[1], sequencer_1_execute_cycle_2, t5_load_b_out_2);
  and t6_enable_alu_out (t6_enable_alu_out_out, t6_enable_alu_out_2, sequencer_1_execute_cycle_3);
  and t6_jump_pc_out (t6_jump_pc_out_out, sequencer_1_execute_cycle_3, t6_jump_pc_out_2);
  or g_enable_alu (ALU[0], t4_enable_alu_out_out, t6_enable_alu_out_out);
  or g_jump_pc (PC[2], t4_jump_pc_out_2, t6_jump_pc_out_out);
  or g_en_pc_out (PC[0], sequencer_1_fetch_set_pc, t4_jump_pc_out_out);
  or g_en_mar_in (MAR[0], sequencer_1_fetch_set_pc, t4_en_mar_in_out);
  or g_en_mar_out (MAR[1], PC[1], t4_en_mar_in_out);
  or g_ram_out (RAM[1], PC[1], t4_ram_load_out);
  or g_en_mdr_out (MDR[1], IR[0], t5_en_mdr_out_out_out);
  or g_en_mdr_in (MDR[0], PC[1], t4_mdr_in_out);
  or g_immediate (g_immediate_out, t4_immediate_out, t5_immediate_out);

  assign IR[1] = IO[3];
  assign MAR[2] = IO[3];
  assign MDR[2] = IO[3];
  assign PC[4] = IO[3];
  assign REG_A[2] = IO[3];
  assign REG_B[2] = IO[3];

  // Notes on the sheet:
  //   DEVICE IO
  //   Fetch dependent Control Matrix
  //   Execution dependent Control Matrix
  //   ALU OPCODES
  //   JUMP OPCODES
  //   status registers
  //   t5
  //   t4
  //   t2
  //   t1
  //   t6
  //   t3
  //   Decode
  //   Execute
  //   Fetch
  //   Decode stage is used mainly for syncronizing gates for inst and interrupts
  //   g_pc_inc
  //   g_en_ir_in
endmodule

module sequencer (
  input  enSEQ,
  input  [3:0] op_in,
  input  stepCLK,
  input  CLK,
  input  reset,
  output halt_out,
  output fetch_set_pc,
  output fetch_cpy_inst,
  output fetch_set_ir,
  output decode,
  output execute_cycle_1,
  output execute_cycle_2,
  output execute_cycle_3,
  output control_decoder_en
);

  wire and_1_out, and_2_out, comparator_1_eq, d_ff_1_q, d_ff_2_q, d_ff_3_q, half_adder_1_sum,
       half_adder_2_cout, half_adder_2_sum, half_adder_3_cout, half_adder_3_sum, or_2_out, or_3_out,
       or_4_out, or_5_out, or_6_out;

  or or_1 (control_decoder_en, execute_cycle_3, execute_cycle_2, execute_cycle_1, decode);
  and and_1 (and_1_out, enSEQ, CLK);
  or or_2 (or_2_out, fetch_set_pc, fetch_cpy_inst, fetch_set_ir);
  LED led_1 (.in(or_2_out));
  LED led_2 (.in(decode));
  or or_3 (or_3_out, stepCLK, and_1_out);
  or or_4 (or_4_out, execute_cycle_1, execute_cycle_2, execute_cycle_3);
  LED led_3 (.in(or_4_out));
  half_adder half_adder_1 (.A(d_ff_1_q), .B(half_adder_2_cout), .Sum(half_adder_1_sum));  // open: Cout
  D_Flip_Flop d_ff_1 (.D(half_adder_1_sum), .clk(or_3_out), .Q(d_ff_1_q), .reset(or_5_out));  // open: Qn, preset
  or or_5 (or_5_out, reset, and_2_out);
  nor nor_1 (fetch_set_pc, d_ff_1_q, d_ff_2_q, d_ff_3_q);
  nor nor_2 (fetch_cpy_inst, d_ff_1_q, d_ff_2_q, ~d_ff_3_q);  // NOR_Gate
  nor nor_3 (fetch_set_ir, d_ff_1_q, ~d_ff_2_q, d_ff_3_q);  // NOR_Gate
  nor nor_4 (decode, d_ff_1_q, ~d_ff_2_q, ~d_ff_3_q);  // NOR_Gate
  nor nor_5 (execute_cycle_1, ~d_ff_1_q, d_ff_2_q, d_ff_3_q);  // NOR_Gate
  nor nor_6 (execute_cycle_2, ~d_ff_1_q, d_ff_2_q, ~d_ff_3_q);  // NOR_Gate
  nor nor_7 (execute_cycle_3, ~d_ff_1_q, ~d_ff_2_q, d_ff_3_q);  // NOR_Gate
  and and_2 (and_2_out, d_ff_1_q, d_ff_2_q, d_ff_3_q);
  half_adder half_adder_2 (.A(d_ff_2_q), .B(half_adder_3_cout), .Sum(half_adder_2_sum), .Cout(half_adder_2_cout));
  D_Flip_Flop d_ff_2 (.D(half_adder_2_sum), .clk(or_3_out), .Q(d_ff_2_q), .reset(or_5_out));  // open: Qn, preset
  LED led_4 (.in(d_ff_1_q));
  half_adder half_adder_3 (.A(d_ff_3_q), .B(or_6_out), .Sum(half_adder_3_sum), .Cout(half_adder_3_cout));
  D_Flip_Flop d_ff_3 (.D(half_adder_3_sum), .clk(or_3_out), .Q(d_ff_3_q), .reset(or_5_out));  // open: Qn, preset
  LED led_5 (.in(d_ff_2_q));
  or or_6 (or_6_out, enSEQ, ~halt_out);  // OR_Gate
  LED led_6 (.in(d_ff_3_q));
  and and_3 (halt_out, comparator_1_eq, execute_cycle_1);
  Comparator #(.mode("unsigned"), .width(4)) comparator_1 (
    .a(4'b0000), .b(op_in), .eq(comparator_1_eq));  // open: gt, lt

  // Notes on the sheet:
  //   Increment by adding the previous state
endmodule

module con (
  input  [15:0] dataIR,
  input  clk,
  input  [2:0] seq_con,
  input  [7:0] flagsIN,
  output [2:0] cmdr,
  output [2:0] c_pc,
  output [1:0] cmar,
  output cirIN,
  output cirRT,
  output [1:0] cram,
  output [2:0] cdio,
  output [3:0] regin_0_3,
  output [15:0] addrOT,
  output [3:0] regin_4_7,
  output [1:0] regin_8_9,
  output [3:0] regot_0_3,
  output [3:0] regot_4_7,
  output [1:0] regot_8_9,
  output [2:0] aluopcode,
  output select_y_4
);

  wire ALUin, buzzer_1_p1, const_ot, decoder_1_out1, decoder_1_out2, decoder_1_out3, decoder_1_out4,
       decoder_1_out5, decoder_1_out6, decoder_1_out8, decoder_1_out9, decoder_1_out10, decoder_1_out11,
       decoder_1_out12, decoder_1_out13, or_2_out, or_3_out, or_4_out, or_5_out, or_6_out, or_7_out,
       or_8_out, or_9_out, or_10_out, or_11_out, or_12_out, or_13_out, or_14_out, or_15_out, or_16_out,
       or_17_out, or_18_out, or_19_out, reg1_in, reg1_ot, reg2_in, reg2_ot, select_const_b,
       sequencer_1_control_decoder_en, sequencer_1_decode, sequencer_1_execute_cycle_1,
       sequencer_1_execute_cycle_2, sequencer_1_execute_cycle_3, sequencer_1_fetch_cpy_inst,
       sequencer_1_fetch_set_ir, sequencer_1_fetch_set_pc, t1_out, t4, t5, t6;
  wire [3:0] multiplexer_1_out, multiplexer_2_out, multiplexer_3_out;
  wire [7:0] multiplexer_4_out;

  sequencer sequencer_1 (
    .op_in(dataIR[15:12]), .enSEQ(seq_con[0]), .stepCLK(seq_con[1]), .CLK(clk), .reset(seq_con[2]),
    .control_decoder_en(sequencer_1_control_decoder_en), .fetch_set_pc(sequencer_1_fetch_set_pc),
    .fetch_cpy_inst(sequencer_1_fetch_cpy_inst), .fetch_set_ir(sequencer_1_fetch_set_ir),
    .decode(sequencer_1_decode), .execute_cycle_1(sequencer_1_execute_cycle_1),
    .execute_cycle_2(sequencer_1_execute_cycle_2), .execute_cycle_3(sequencer_1_execute_cycle_3),
    .halt_out(c_pc[2]));
  Hex_Digit_Display hex_digit_display_1 (.value(dataIR[15:12]));  // open: dp
  Hex_Digit_Display hex_digit_display_2 (.value(dataIR[11:8]));  // open: dp
  Decoder #(.select(4)) decoder_1 (
    .out1(decoder_1_out1), .out2(decoder_1_out2), .out3(decoder_1_out3), .out4(decoder_1_out4),
    .out5(decoder_1_out5), .out6(decoder_1_out6), .out8(decoder_1_out8), .out9(decoder_1_out9),
    .out10(decoder_1_out10), .out11(decoder_1_out11), .out12(decoder_1_out12), .out13(decoder_1_out13),
    .sel(dataIR[15:12]), .en(sequencer_1_control_decoder_en));  // open: out0, out7, out14, out15
  or or_1 (c_pc[1], buzzer_1_p1, t1_out);
  or or_2 (or_2_out, decoder_1_out6, decoder_1_out5, decoder_1_out3, decoder_1_out2);
  controlled_timer controlled_timer_1 (
    .t4_in(t4), .t5_in(t5), .t6_in(t6), .t4_or(or_2_out), .trest_or(buzzer_1_p1), .tm_or(cmar[0]));  // open: t5_or, t6_or
  controlled_timer controlled_timer_2 (
    .t4_in(t4), .t5_in(t5), .t6_in(t6), .t5_or(or_10_out), .t6_or(or_11_out), .trest_or(t1_out),
    .tm_or(cmar[1]));  // open: t4_or
  controlled_timer controlled_timer_3 (
    .t4_in(t4), .t5_in(t5), .t6_in(t6), .t5_or(or_3_out), .trest_or(t1_out), .tm_or(cmdr[0]));  // open: t4_or, t6_or
  or or_3 (or_3_out, decoder_1_out6, decoder_1_out5, decoder_1_out3, decoder_1_out2);
  controlled_timer controlled_timer_4 (
    .t4_in(t4), .t5_in(t5), .t6_in(t6), .t5_or(decoder_1_out3), .t6_or(or_4_out), .tm_or(cmdr[1]));  // open: t4_or, trest_or
  or or_4 (or_4_out, decoder_1_out6, decoder_1_out3);
  controlled_timer controlled_timer_5 (
    .t4_in(t4), .t5_in(t5), .t6_in(t6), .t6_or(or_5_out), .trest_or(select_y_4), .tm_or(cmdr[2]));  // open: t4_or, t5_or
  or or_5 (or_5_out, decoder_1_out6, decoder_1_out5, decoder_1_out3, decoder_1_out2);
  controlled_timer controlled_timer_6 (
    .t4_in(t4), .t5_in(t5), .t6_in(t6), .t6_or(or_6_out), .tm_or(cram[0]));  // open: t4_or, t5_or, trest_or
  or or_6 (or_6_out, decoder_1_out6, decoder_1_out3);
  controlled_timer controlled_timer_7 (
    .t4_in(t4), .t5_in(t5), .t6_in(t6), .t5_or(decoder_1_out2), .trest_or(t1_out), .tm_or(cram[1]));  // open: t4_or, t6_or
  or or_7 (or_7_out, decoder_1_out10, decoder_1_out9, decoder_1_out8);
  controlled_timer controlled_timer_8 (
    .t4_in(t4), .t5_in(t5), .t6_in(t6), .t4_or(or_7_out), .trest_or(t1_out), .tm_or(regin_8_9[0]));  // open: t5_or, t6_or
  controlled_timer controlled_timer_9 (
    .t4_in(t4), .t5_in(t5), .t6_in(t6), .t5_or(or_8_out), .trest_or(select_y_4), .tm_or(regin_8_9[1]));  // open: t4_or, t6_or
  or or_8 (or_8_out, decoder_1_out10, decoder_1_out9, decoder_1_out8);
  controlled_timer controlled_timer_10 (
    .t4_in(t4), .t5_in(t5), .t6_in(t6), .t5_or(or_9_out), .trest_or(select_y_4), .tm_or(regot_8_9[0]));  // open: t4_or, t6_or
  or or_9 (or_9_out, decoder_1_out10, decoder_1_out9, decoder_1_out8);
  controlled_timer controlled_timer_11 (
    .t4_in(t4), .t5_in(t5), .t6_in(t6), .t6_or(or_12_out), .trest_or(c_pc[0]), .tm_or(regot_8_9[1]));  // open: t4_or, t5_or
  controlled_timer controlled_timer_12 (
    .t4_in(t4), .t5_in(t5), .t6_in(t6), .trest_or(select_y_4), .tm_or(cirIN));  // open: t4_or, t5_or, t6_or
  controlled_timer controlled_timer_13 (
    .t4_in(t4), .t5_in(t5), .t6_in(t6), .t4_or(or_13_out), .t6_or(or_14_out), .tm_or(reg1_in));  // open: t5_or, trest_or
  controlled_timer controlled_timer_14 (
    .t4_in(t4), .t5_in(t5), .t6_in(t6), .tm_or(reg2_in));  // open: t4_or, t5_or, t6_or, trest_or
  controlled_timer controlled_timer_15 (
    .t4_in(t4), .t5_in(t5), .t6_in(t6), .t4_or(or_15_out), .tm_or(reg1_ot));  // open: t5_or, t6_or, trest_or
  controlled_timer controlled_timer_16 (
    .t4_in(t4), .t5_in(t5), .t6_in(t6), .t4_or(decoder_1_out4), .t5_or(or_16_out), .tm_or(reg2_ot));  // open: t6_or, trest_or
  controlled_timer controlled_timer_17 (
    .t4_in(t4), .t5_in(t5), .t6_in(t6), .t4_or(or_17_out), .tm_or(const_ot));  // open: t5_or, t6_or, trest_or
  controlled_timer controlled_timer_18 (
    .t4_in(t4), .t5_in(t5), .t6_in(t6), .t4_or(decoder_1_out3), .tm_or(select_const_b));  // open: t5_or, t6_or, trest_or
  Hex_Digit_Display hex_digit_display_3 (.value(dataIR[7:4]));  // open: dp
  // Buzzer buzzer_1: pin names not known; wires that end beside it: buzzer_1_p1, 14'h200, 7'b0000100
  buf t3 (c_pc[0], sequencer_1_decode);
  buf t2 (select_y_4, sequencer_1_fetch_set_ir);
  buf t1 (t1_out, sequencer_1_fetch_cpy_inst);
  buf t0 (buzzer_1_p1, sequencer_1_fetch_set_pc);
  or or_10 (or_10_out, decoder_1_out2, decoder_1_out5);
  or or_11 (or_11_out, decoder_1_out3, decoder_1_out6);
  or or_12 (or_12_out, decoder_1_out10, decoder_1_out9, decoder_1_out8);
  or or_13 (or_13_out, decoder_1_out4, decoder_1_out1);
  or or_14 (or_14_out, decoder_1_out8, decoder_1_out5, decoder_1_out9, decoder_1_out2, decoder_1_out10);
  or or_15 (or_15_out, decoder_1_out8, decoder_1_out9, decoder_1_out10, decoder_1_out6);
  or or_16 (or_16_out, decoder_1_out9, decoder_1_out8, decoder_1_out6, decoder_1_out3);
  or or_17 (or_17_out, decoder_1_out3, decoder_1_out2, decoder_1_out1);
  Hex_Digit_Display hex_digit_display_4 (.value(dataIR[3:0]));  // open: dp
  buf u_t6 (t6, sequencer_1_execute_cycle_3);
  buf u_t5 (t5, sequencer_1_execute_cycle_2);
  buf u_t4 (t4, sequencer_1_execute_cycle_1);
  or or_18 (or_18_out, reg1_in, reg2_in);
  or or_19 (or_19_out, reg1_ot, reg2_ot);
  Priority_Encoder priority_encoder_1 (
    .in0(decoder_1_out8), .in1(decoder_1_out9), .in2(decoder_1_out10), .in3(decoder_1_out11),
    .in4(decoder_1_out12), .in5(decoder_1_out13), .out(aluopcode), .gs(ALUin));  // open: in6, in7, en_in, en_out
  Multiplexer #(.width(4)) multiplexer_1 (
    .in0(dataIR[11:8]), .in1(dataIR[3:0]), .out(multiplexer_1_out), .sel(reg2_in));
  Multiplexer #(.width(4)) multiplexer_2 (
    .in0(dataIR[11:8]), .in1(dataIR[3:0]), .out(multiplexer_2_out), .sel(reg2_ot));
  Multiplexer #(.width(4)) multiplexer_3 (.in0(multiplexer_1_out), .in1(4'b0000), .out(multiplexer_3_out), .sel(ALUin));
  Decoder #(.disabled("Z"), .select(4)) decoder_2 (
    .out0(regot_0_3[0]), .out1(regot_0_3[1]), .out2(regot_0_3[2]), .out3(regot_0_3[3]), .out4(regot_4_7[0]),
    .out5(regot_4_7[1]), .out6(regot_4_7[2]), .out7(regot_4_7[3]), .sel(multiplexer_2_out), .en(or_19_out));  // open: out8, out9, out10, out11, out12, out13, out14, out15
  Decoder #(.disabled("Z"), .select(4)) decoder_3 (
    .out0(regin_0_3[0]), .out1(regin_0_3[1]), .out2(regin_0_3[2]), .out3(regin_0_3[3]), .out4(regin_4_7[0]),
    .out5(regin_4_7[1]), .out6(regin_4_7[2]), .out7(regin_4_7[3]), .sel(multiplexer_3_out), .en(or_18_out));  // open: out8, out9, out10, out11, out12, out13, out14, out15
  assign addrOT = {{8{multiplexer_4_out[7]}}, multiplexer_4_out};  // Bit_Extender bit_extender_1
  Multiplexer #(.disabled("Z"), .enable("true"), .width(8)) multiplexer_4 (
    .in0(dataIR[7:0]), .in1(dataIR[11:4]), .out(multiplexer_4_out), .sel(select_const_b), .en(const_ot));

  assign cirRT = c_pc[2];

  // Other names for the same wires on the sheet: cpcIN = c_pc[0]; cpcOT = c_pc[1]; cdioIn = cdio[0]; cdioOT = cdio[1];
  //   cdioDI = cdio[2]; cmarIN = cmar[0]; cmarOT = cmar[1]; cmdrIN = cmdr[0]; cmdrRAM = cmdr[1]; cmdrOT = cmdr[2];
  //   cramIN = cram[0]; cramOT = cram[1]; flags[7:0] = flagsIN

  // Notes on the sheet:
  //   Opcode Area
  //   Decodes the opcode to micrcode, then 
  //   schedules execution by the FDS cycle
  //   Fetch
  //   Decode
  //   Execute
endmodule

module sap_cpu (
);

  arithmetic_logic_unit arithmetic_logic_unit_1 ();  // open: alu_op, A, B, enALU, Result, status
endmodule

module memory (
  input  clkIN,
  input  [15:0] addrIN,
  input  [1:0] contRM,
  input  [15:0] ramOUT,
  input  [15:0] dataIN,
  output clkRAM,
  output [7:0] addrRAM,
  output writeRAM,
  output [15:0] dataOUT,
  output [15:0] ramIN
);

  Bit_Extender #(.in_width(16), .out_width(8)) bit_extender_1 (.in(addrIN), .out(addrRAM));
  Pull_Resistor pull_resistor_1 (.node(dataIN));
  Hex_Digit_Display hex_digit_display_1 (.value(addrRAM[7:4]));  // open: dp
  LED led_1 (.in(contRM[0]));
  LED led_2 (.in(contRM[1]));
  Hex_Digit_Display hex_digit_display_2 (.value(addrRAM[3:0]));  // open: dp
  Hex_Digit_Display hex_digit_display_3 (.value(dataIN[15:12]));  // open: dp
  Hex_Digit_Display hex_digit_display_4 (.value(dataIN[11:8]));  // open: dp
  Hex_Digit_Display hex_digit_display_5 (.value(ramOUT[15:12]));  // open: dp
  Hex_Digit_Display hex_digit_display_6 (.value(ramOUT[11:8]));  // open: dp
  Hex_Digit_Display hex_digit_display_7 (.value(dataIN[7:4]));  // open: dp
  Hex_Digit_Display hex_digit_display_8 (.value(dataIN[3:0]));  // open: dp
  Hex_Digit_Display hex_digit_display_9 (.value(ramOUT[7:4]));  // open: dp
  Hex_Digit_Display hex_digit_display_10 (.value(ramOUT[3:0]));  // open: dp

  assign clkRAM = clkIN;
  assign dataOUT = ramOUT;
  assign ramIN = dataIN;
  assign writeRAM = contRM[0];
endmodule

module carrylookahead (
  input  p3,
  input  g3,
  input  p2,
  input  g2,
  input  p1,
  input  g1,
  input  p0,
  input  g0,
  input  c0,
  output c4,
  output s3,
  output s2,
  output s1,
  output s0
);

  wire and_1_out, and_2_out, and_3_out, and_4_out, and_5_out, and_6_out, and_7_out, and_8_out, and_9_out,
       and_10_out, and_11_out, and_12_out, and_13_out, and_14_out, or_2_out, or_3_out, or_4_out, xor_1_out,
       xor_2_out, xor_3_out, xor_4_out;

  xor xor_1 (xor_1_out, p3, g3);
  and and_1 (and_1_out, p3, g3);
  xor xor_2 (xor_2_out, p2, g2);
  and and_2 (and_2_out, p2, g2);
  xor xor_3 (xor_3_out, p1, g1);
  and and_3 (and_3_out, p1, g1);
  xor xor_4 (xor_4_out, p0, g0);
  and and_4 (and_4_out, p0, g0);
  and and_5 (and_5_out, c0, xor_4_out, xor_3_out, xor_2_out, xor_1_out);
  and and_6 (and_6_out, and_4_out, xor_3_out, xor_2_out, xor_1_out);
  and and_7 (and_7_out, and_3_out, xor_2_out, xor_1_out);
  and and_8 (and_8_out, and_2_out, xor_1_out);
  and and_9 (and_9_out, c0, xor_4_out, xor_3_out, xor_2_out);
  and and_10 (and_10_out, and_4_out, xor_3_out, xor_2_out);
  and and_11 (and_11_out, and_3_out, xor_2_out);
  and and_12 (and_12_out, c0, xor_4_out, xor_3_out);
  and and_13 (and_13_out, and_4_out, xor_3_out);
  and and_14 (and_14_out, c0, xor_4_out);
  or or_1 (c4, and_5_out, and_6_out, and_7_out, and_8_out, and_1_out);
  xor xor_5 (s3, xor_1_out, or_2_out);
  or or_2 (or_2_out, and_9_out, and_10_out, and_11_out, and_2_out);
  xor xor_6 (s2, xor_2_out, or_3_out);
  or or_3 (or_3_out, and_12_out, and_13_out, and_3_out);
  xor xor_7 (s1, xor_3_out, or_4_out);
  or or_4 (or_4_out, and_14_out, and_4_out);
  xor xor_8 (s0, xor_4_out, c0);
endmodule

module addsub4 (
  input  [3:0] a,
  input  [3:0] b,
  input  xor_en,
  input  cin,
  output [3:0] s,
  output zero,
  output cout
);

  wire xor_1_out, xor_2_out, xor_3_out, xor_4_out;

  xor xor_1 (xor_1_out, b[3], xor_en);
  xor xor_2 (xor_2_out, b[2], xor_en);
  xor xor_3 (xor_3_out, b[1], xor_en);
  xor xor_4 (xor_4_out, b[0], xor_en);
  carrylookahead carrylookahead_1 (
    .p0(a[0]), .g0(xor_4_out), .p3(a[3]), .g3(xor_1_out), .p2(a[2]), .g2(xor_2_out), .p1(a[1]),
    .g1(xor_3_out), .c0(cin), .s1(s[1]), .s0(s[0]), .c4(cout), .s3(s[3]), .s2(s[2]));
  nor nor_1 (zero, s[3], s[2], s[1], s[0]);
endmodule

module addsub16 (
  input  [15:0] a,
  input  [15:0] b,
  input  invert,
  input  cin,
  output cout,
  output [15:0] out_6,
  output overflow,
  output aux_flag,
  output zero_flag
);

  wire addsub4_1_zero, addsub4_2_cout, addsub4_2_zero, addsub4_3_cout, addsub4_3_zero, addsub4_4_zero;

  addsub4 addsub4_1 (
    .a(a[3:0]), .b(b[3:0]), .xor_en(invert), .cin(addsub4_2_cout), .cout(cout), .zero(addsub4_1_zero),
    .s(out_6[3:0]));
  addsub4 addsub4_2 (
    .a(a[7:4]), .b(b[7:4]), .xor_en(invert), .cin(addsub4_3_cout), .cout(addsub4_2_cout),
    .zero(addsub4_2_zero), .s(out_6[7:4]));
  addsub4 addsub4_3 (
    .a(a[11:8]), .b(b[11:8]), .xor_en(invert), .cin(aux_flag), .cout(addsub4_3_cout), .zero(addsub4_3_zero),
    .s(out_6[11:8]));
  addsub4 addsub4_4 (
    .a(a[15:12]), .b(b[15:12]), .xor_en(invert), .cin(cin), .cout(aux_flag), .zero(addsub4_4_zero),
    .s(out_6[15:12]));
  xor xor_1 (overflow, cout, addsub4_1_zero);
  and and_1 (zero_flag, addsub4_1_zero, addsub4_2_zero, addsub4_3_zero, addsub4_4_zero);
endmodule

module part_adder (
  input  a,
  input  b,
  input  c_in,
  output S,
  output P_i,
  output G_i
);

  wire xor_1_out;

  xor xor_1 (xor_1_out, a, b);
  xor xor_2 (S, xor_1_out, c_in);
  or or_1 (P_i, a, b);
  and and_1 (G_i, a, b);
endmodule

module controlled_timer (
  input  t4_in,
  input  t5_in,
  input  t6_in,
  input  t4_or,
  input  t5_or,
  input  t6_or,
  input  trest_or,
  output tm_or
);

  wire and_1_out, and_2_out, and_3_out;

  and and_1 (and_1_out, t4_in, t4_or);
  and and_2 (and_2_out, t5_in, t5_or);
  and and_3 (and_3_out, t6_in, t6_or);
  or or_1 (tm_or, and_1_out, and_2_out, and_3_out, trest_or);
endmodule

module block_memory (
  input  [1:0] mar_control,
  input  clk,
  input  [15:0] in_3,
  input  [15:0] ramDOUT,
  input  [2:0] mdr_control,
  output [15:0] ramIOUT,
  output [15:0] ramDIN,
  output [15:0] out_8
);

  memory_data_register memory_data_register_1 (
    .ramIN(ramDOUT), .dIN(in_3), .enIN(mdr_control[0]), .enRAM(mdr_control[1]), .erOT(mdr_control[2]),
    .clk(clk), .reset(1'b0), .dOUT(out_8), .ramOUT(ramDIN));
  memory_address_register memory_address_register_1 (
    .dBUS(in_3), .enIN(mar_control[0]), .clk(clk), .reset(1'b0), .enOUT(mar_control[1]), .dRAM(ramIOUT));
endmodule

module reg_left_2 (
  input  clk,
  input  [15:0] datain,
  input  load,
  input  reset,
  input  store,
  output [15:0] dataout
);

  wire [15:0] pull_resistor_1_node, register_1_q;

  Pull_Resistor pull_resistor_1 (.node(pull_resistor_1_node));
  assign pull_resistor_1_node = load ? datain : 16'bz;  // Controlled_Buffer controlled_buffer_1
  Register #(.width(16)) register_1 (.D(pull_resistor_1_node), .en(load), .clk(clk), .Q(register_1_q), .clr(reset));
  Hex_Digit_Display hex_digit_display_1 (.value(register_1_q[15:12]));  // open: dp
  assign dataout = store ? register_1_q : 16'bz;  // Controlled_Buffer controlled_buffer_2
  Hex_Digit_Display hex_digit_display_2 (.value(register_1_q[11:8]));  // open: dp
  Hex_Digit_Display hex_digit_display_3 (.value(register_1_q[7:4]));  // open: dp
  Hex_Digit_Display hex_digit_display_4 (.value(register_1_q[3:0]));  // open: dp
endmodule

module reg_right_2 (
  input  clk,
  input  [15:0] datain,
  input  [2:0] pc,
  output [15:0] dataout
);

  wire [15:0] controlled_buffer_1_out, register_1_q;

  assign controlled_buffer_1_out = pc[0] ? datain : 16'bz;  // Controlled_Buffer controlled_buffer_1
  Register #(.width(16)) register_1 (.D(controlled_buffer_1_out), .en(pc[0]), .clk(clk), .Q(register_1_q), .clr(pc[2]));
  Hex_Digit_Display hex_digit_display_1 (.value(register_1_q[15:12]));  // open: dp
  assign dataout = pc[1] ? register_1_q : 16'bz;  // Controlled_Buffer controlled_buffer_2
  Hex_Digit_Display hex_digit_display_2 (.value(register_1_q[11:8]));  // open: dp
  Hex_Digit_Display hex_digit_display_3 (.value(register_1_q[7:4]));  // open: dp
  Hex_Digit_Display hex_digit_display_4 (.value(register_1_q[3:0]));  // open: dp
endmodule

module zero_negative_identify (
  input  [15:0] datain,
  output zero,
  output negative
);

  or or_1 (zero, datain[0], datain[1], datain[2], datain[3], datain[4], datain[5], datain[6], datain[7], datain[9], datain[10], datain[11], datain[12], datain[13], datain[14], datain[15], datain[8]);

  assign negative = datain[15];
endmodule

module block_register_4 (
  input  clk,
  input  [15:0] regin,
  input  [3:0] regin_4,
  input  [3:0] regot_4,
  input  reset,
  output [15:0] regout
);

  reg_left_2 reg_left_2_1 (
    .datain(regin), .clk(clk), .load(regin_4[0]), .reset(reset), .store(regot_4[0]), .dataout(regout));
  reg_left_2 reg_left_2_2 (
    .datain(regin), .clk(clk), .load(regin_4[1]), .reset(reset), .store(regot_4[1]), .dataout(regout));
  reg_left_2 reg_left_2_3 (
    .datain(regin), .clk(clk), .load(regin_4[2]), .reset(reset), .store(regot_4[2]), .dataout(regout));
  reg_left_2 reg_left_2_4 (
    .datain(regin), .clk(clk), .load(regin_4[3]), .reset(reset), .store(regot_4[3]), .dataout(regout));
endmodule

module block_logic (
  input  [15:0] datain,
  input  clk,
  input  [1:0] regin,
  input  select_y_4,
  input  [2:0] aluopcode,
  input  [1:0] regot,
  input  reset,
  output [15:0] dataot,
  output [7:0] flags
);

  wire [15:0] arithmetic_logic_unit_1_result, multiplexer_1_out, reg_left_2_1_dataout;

  reg_left_2 reg_left_2_1 (
    .datain(datain), .clk(clk), .load(regin[0]), .reset(reset), .store(regot[0]),
    .dataout(reg_left_2_1_dataout));
  reg_left_2 reg_left_2_2 (
    .datain(arithmetic_logic_unit_1_result), .clk(clk), .load(regin[1]), .reset(reset), .store(regot[1]),
    .dataout(dataot));
  Pull_Resistor pull_resistor_1 (.node(reg_left_2_1_dataout));
  Multiplexer #(.width(16)) multiplexer_1 (.in0(datain), .in1(16'h1), .out(multiplexer_1_out), .sel(select_y_4));
  Pull_Resistor pull_resistor_2 (.node(multiplexer_1_out));
  arithmetic_logic_unit arithmetic_logic_unit_1 (
    .alu_op(aluopcode), .A(reg_left_2_1_dataout), .B(multiplexer_1_out), .enALU(regin[1]),
    .Result(arithmetic_logic_unit_1_result), .status(flags));

  // Other names for the same wires on the sheet: enZ = regin[1]
endmodule

module control_matrix (
);

  wire ALUin, cirIn, cmarIN, cmarOT, cmdrIN, cmdrOT, cmdrRAM, const_ot, cpcIN, cpcOT, cramIN, cramOT,
       decoder_1_out1, decoder_1_out2, decoder_1_out3, decoder_1_out4, decoder_1_out5, decoder_1_out6,
       decoder_1_out8, decoder_1_out9, decoder_1_out10, decoder_1_out11, decoder_1_out12, decoder_1_out13,
       or_2_out, or_3_out, or_4_out, or_5_out, or_6_out, or_7_out, or_8_out, or_9_out, or_10_out, or_11_out,
       or_12_out, or_13_out, or_14_out, or_15_out, or_16_out, or_17_out, reg1_in, reg1_ot, reg2_in, reg2_ot,
       select_const_b, t4, t5, t6, undriven_2, undriven_3, undriven_4;
  wire [1:0] regin_8_9, regot_8_9;
  wire [2:0] priority_encoder_1_out;
  wire [3:0] undriven;

  Decoder #(.select(4)) decoder_1 (
    .out1(decoder_1_out1), .out2(decoder_1_out2), .out3(decoder_1_out3), .out4(decoder_1_out4),
    .out5(decoder_1_out5), .out6(decoder_1_out6), .out8(decoder_1_out8), .out9(decoder_1_out9),
    .out10(decoder_1_out10), .out11(decoder_1_out11), .out12(decoder_1_out12), .out13(decoder_1_out13),
    .sel(undriven));  // open: out0, out7, out14, out15, en
  or or_1 (cpcOT, undriven_2, undriven_3);
  or or_2 (or_2_out, decoder_1_out6, decoder_1_out5, decoder_1_out3, decoder_1_out2);
  controlled_timer controlled_timer_1 (
    .t4_in(t4), .t5_in(t5), .t6_in(t6), .t4_or(or_2_out), .trest_or(undriven_2), .tm_or(cmarIN));  // open: t5_or, t6_or
  controlled_timer controlled_timer_2 (
    .t4_in(t4), .t5_in(t5), .t6_in(t6), .t5_or(or_10_out), .t6_or(or_11_out), .trest_or(undriven_3),
    .tm_or(cmarOT));  // open: t4_or
  controlled_timer controlled_timer_3 (
    .t4_in(t4), .t5_in(t5), .t6_in(t6), .t5_or(or_3_out), .trest_or(undriven_3), .tm_or(cmdrIN));  // open: t4_or, t6_or
  or or_3 (or_3_out, decoder_1_out6, decoder_1_out5, decoder_1_out3, decoder_1_out2);
  controlled_timer controlled_timer_4 (
    .t4_in(t4), .t5_in(t5), .t6_in(t6), .t5_or(decoder_1_out3), .t6_or(or_4_out), .tm_or(cmdrRAM));  // open: t4_or, trest_or
  or or_4 (or_4_out, decoder_1_out6, decoder_1_out3);
  controlled_timer controlled_timer_5 (
    .t4_in(t4), .t5_in(t5), .t6_in(t6), .t6_or(or_5_out), .trest_or(undriven_4), .tm_or(cmdrOT));  // open: t4_or, t5_or
  or or_5 (or_5_out, decoder_1_out6, decoder_1_out5, decoder_1_out3, decoder_1_out2);
  controlled_timer controlled_timer_6 (
    .t4_in(t4), .t5_in(t5), .t6_in(t6), .t6_or(or_6_out), .tm_or(cramIN));  // open: t4_or, t5_or, trest_or
  or or_6 (or_6_out, decoder_1_out6, decoder_1_out3);
  controlled_timer controlled_timer_7 (
    .t4_in(t4), .t5_in(t5), .t6_in(t6), .t5_or(decoder_1_out2), .trest_or(undriven_3), .tm_or(cramOT));  // open: t4_or, t6_or
  or or_7 (or_7_out, decoder_1_out10, decoder_1_out9, decoder_1_out8);
  controlled_timer controlled_timer_8 (
    .t4_in(t4), .t5_in(t5), .t6_in(t6), .t4_or(or_7_out), .trest_or(undriven_3), .tm_or(regin_8_9[0]));  // open: t5_or, t6_or
  controlled_timer controlled_timer_9 (
    .t4_in(t4), .t5_in(t5), .t6_in(t6), .t5_or(or_8_out), .trest_or(undriven_4), .tm_or(regin_8_9[1]));  // open: t4_or, t6_or
  or or_8 (or_8_out, decoder_1_out10, decoder_1_out9, decoder_1_out8);
  controlled_timer controlled_timer_10 (
    .t4_in(t4), .t5_in(t5), .t6_in(t6), .t5_or(or_9_out), .trest_or(undriven_4), .tm_or(regot_8_9[0]));  // open: t4_or, t6_or
  or or_9 (or_9_out, decoder_1_out10, decoder_1_out9, decoder_1_out8);
  controlled_timer controlled_timer_11 (
    .t4_in(t4), .t5_in(t5), .t6_in(t6), .t6_or(or_12_out), .trest_or(cpcIN), .tm_or(regot_8_9[1]));  // open: t4_or, t5_or
  controlled_timer controlled_timer_12 (
    .t4_in(t4), .t5_in(t5), .t6_in(t6), .trest_or(undriven_4), .tm_or(cirIn));  // open: t4_or, t5_or, t6_or
  controlled_timer controlled_timer_13 (
    .t4_in(t4), .t5_in(t5), .t6_in(t6), .t4_or(or_13_out), .t6_or(or_14_out), .tm_or(reg1_in));  // open: t5_or, trest_or
  controlled_timer controlled_timer_14 (
    .t4_in(t4), .t5_in(t5), .t6_in(t6), .tm_or(reg2_in));  // open: t4_or, t5_or, t6_or, trest_or
  controlled_timer controlled_timer_15 (
    .t4_in(t4), .t5_in(t5), .t6_in(t6), .t4_or(or_15_out), .tm_or(reg1_ot));  // open: t5_or, t6_or, trest_or
  controlled_timer controlled_timer_16 (
    .t4_in(t4), .t5_in(t5), .t6_in(t6), .t4_or(decoder_1_out4), .t5_or(or_16_out), .tm_or(reg2_ot));  // open: t6_or, trest_or
  controlled_timer controlled_timer_17 (
    .t4_in(t4), .t5_in(t5), .t6_in(t6), .t4_or(or_17_out), .tm_or(const_ot));  // open: t5_or, t6_or, trest_or
  controlled_timer controlled_timer_18 (
    .t4_in(t4), .t5_in(t5), .t6_in(t6), .t4_or(decoder_1_out3), .tm_or(select_const_b));  // open: t5_or, t6_or, trest_or
  or or_10 (or_10_out, decoder_1_out2, decoder_1_out5);
  or or_11 (or_11_out, decoder_1_out3, decoder_1_out6);
  or or_12 (or_12_out, decoder_1_out10, decoder_1_out9, decoder_1_out8);
  or or_13 (or_13_out, decoder_1_out4, decoder_1_out1);
  or or_14 (or_14_out, decoder_1_out8, decoder_1_out5, decoder_1_out9, decoder_1_out2, decoder_1_out10);
  or or_15 (or_15_out, decoder_1_out8, decoder_1_out9, decoder_1_out10, decoder_1_out6);
  or or_16 (or_16_out, decoder_1_out9, decoder_1_out8, decoder_1_out6, decoder_1_out3);
  or or_17 (or_17_out, decoder_1_out3, decoder_1_out2, decoder_1_out1);
  Priority_Encoder priority_encoder_1 (
    .in0(decoder_1_out8), .in1(decoder_1_out9), .in2(decoder_1_out10), .in3(decoder_1_out11),
    .in4(decoder_1_out12), .in5(decoder_1_out13), .out(priority_encoder_1_out), .gs(ALUin));  // open: in6, in7, en_in, en_out

  // Notes on the sheet:
  //   Opcode Area
  //   Decodes the opcode to micrcode, then 
  //   schedules execution by the FDS cycle
endmodule

// VHDL entity contest, as the project stores it:
--------------------------------------------------------------------------------
-- Project :
-- File    :
-- Autor   :
-- Date    :
--
--------------------------------------------------------------------------------
-- Description :
--
--------------------------------------------------------------------------------

LIBRARY ieee;
USE ieee.std_logic_1164.all;

ENTITY contest IS
  PORT (
  ------------------------------------------------------------------------------
  --Insert input ports below
    clock      : IN  std_logic;                    -- input bit example
    val        : IN  std_logic_vector(3 DOWNTO 0); -- input vector example
  ------------------------------------------------------------------------------
  --Insert output ports below
    max        : OUT std_logic;                    -- output bit example
    cpt        : OUT std_logic_vector(3 DOWNTO 0)  -- output vector example
    );
END contest;

--------------------------------------------------------------------------------
--Complete your VHDL description below
--------------------------------------------------------------------------------

ARCHITECTURE TypeArchitecture OF contest IS

BEGIN


END TypeArchitecture;
