// Logisim project nibbles.circ as structural Verilog: 12 circuits, main circuit main
module main (
);

  wire undriven, undriven_2;
  wire [63:0] block_alu_1_dataout, block_reg_16_1_dataout;

  block_reg_16 block_reg_16_1 (
    .clock(undriven), .reset(undriven_2), .DATAin(block_alu_1_dataout), .DATAout(block_reg_16_1_dataout));  // open: RLin, RHin, RXin, ERXin, RRXin, RLout, RHout, RXout, ERXout, RRXout
  block_ALU block_alu_1 (
    .DATAin(block_reg_16_1_dataout), .clock(undriven), .reset(undriven_2), .DATAout(block_alu_1_dataout));  // open: ZREGin, Select4, SelectY, YREGin, CMC, enableALU, SETC, CLC, aluOPCODE
endmodule

module block_reg_16 (
  input  clock,
  input  reset,
  input  [63:0] DATAin,
  input  [15:0] RLin,
  input  [15:0] RLout,
  input  [15:0] RHin,
  input  [15:0] RHout,
  input  [15:0] RXin,
  input  [15:0] RXout,
  input  [15:0] ERXin,
  input  [15:0] ERXout,
  input  [15:0] RRXin,
  input  [15:0] RRXout,
  output [63:0] DATAout
);

  wire undriven, undriven_2, undriven_3, undriven_4, undriven_5, undriven_6, undriven_7, undriven_8,
       undriven_9, undriven_10, undriven_11, undriven_12, undriven_13, undriven_14, undriven_15, undriven_16,
       undriven_17, undriven_18, undriven_19, undriven_20, undriven_21, undriven_22, undriven_23,
       undriven_24, undriven_25, undriven_26, undriven_27, undriven_28, undriven_29, undriven_30,
       undriven_31, undriven_32, undriven_33, undriven_34, undriven_35, undriven_36, undriven_37,
       undriven_38, undriven_39, undriven_40, undriven_41, undriven_42, undriven_43, undriven_44,
       undriven_45, undriven_46, undriven_47, undriven_48, undriven_49, undriven_50, undriven_51,
       undriven_52, undriven_53, undriven_54, undriven_55, undriven_56, undriven_57, undriven_58,
       undriven_59, undriven_60, undriven_61, undriven_62, undriven_63, undriven_64, undriven_65,
       undriven_66, undriven_67, undriven_68, undriven_69, undriven_70, undriven_71, undriven_72,
       undriven_73, undriven_74, undriven_75, undriven_76, undriven_77, undriven_78, undriven_79,
       undriven_80, undriven_81, undriven_82, undriven_83, undriven_84, undriven_85, undriven_86,
       undriven_87, undriven_88, undriven_89, undriven_90, undriven_91, undriven_92, undriven_93,
       undriven_94, undriven_95, undriven_96, undriven_97, undriven_98, undriven_99, undriven_100,
       undriven_101, undriven_102, undriven_103, undriven_104, undriven_105, undriven_106, undriven_107,
       undriven_108, undriven_109, undriven_110, undriven_111, undriven_112, undriven_113, undriven_114,
       undriven_115, undriven_116, undriven_117, undriven_118, undriven_119, undriven_120, undriven_121,
       undriven_122, undriven_123, undriven_124, undriven_125, undriven_126, undriven_127, undriven_128,
       undriven_129, undriven_130, undriven_131, undriven_132, undriven_133, undriven_134, undriven_135,
       undriven_136, undriven_137, undriven_138, undriven_139, undriven_140, undriven_141, undriven_142,
       undriven_143, undriven_144, undriven_145, undriven_146, undriven_147, undriven_148, undriven_149,
       undriven_150, undriven_151, undriven_152, undriven_153, undriven_154, undriven_155, undriven_156,
       undriven_157, undriven_158, undriven_159, undriven_160;

  block_reg_sizes RAX (
    .RLin(undriven), .RHin(undriven_2), .RXin(undriven_3), .ERXin(undriven_4), .RRXin(undriven_5),
    .RLout(undriven_81), .RHout(undriven_82), .RXout(undriven_83), .ERXout(undriven_84),
    .RRXout(undriven_85), .in_1(DATAin), .clock(clock), .reset(reset), .out_14(DATAout));
  block_reg_sizes RBX (
    .RLin(undriven_6), .RHin(undriven_7), .RXin(undriven_8), .ERXin(undriven_9), .RRXin(undriven_10),
    .RLout(undriven_86), .RHout(undriven_87), .RXout(undriven_88), .ERXout(undriven_89),
    .RRXout(undriven_90), .in_1(DATAin), .clock(clock), .reset(reset), .out_14(DATAout));
  block_reg_sizes RCX (
    .RLin(undriven_11), .RHin(undriven_12), .RXin(undriven_13), .ERXin(undriven_14), .RRXin(undriven_15),
    .RLout(undriven_91), .RHout(undriven_92), .RXout(undriven_93), .ERXout(undriven_94),
    .RRXout(undriven_95), .in_1(DATAin), .clock(clock), .reset(reset), .out_14(DATAout));
  block_reg_sizes RDX (
    .RLin(undriven_16), .RHin(undriven_17), .RXin(undriven_18), .ERXin(undriven_19), .RRXin(undriven_20),
    .RLout(undriven_96), .RHout(undriven_97), .RXout(undriven_98), .ERXout(undriven_99),
    .RRXout(undriven_100), .in_1(DATAin), .clock(clock), .reset(reset), .out_14(DATAout));
  block_reg_sizes RSP (
    .RLin(undriven_21), .RHin(undriven_22), .RXin(undriven_23), .ERXin(undriven_24), .RRXin(undriven_25),
    .RLout(undriven_101), .RHout(undriven_102), .RXout(undriven_103), .ERXout(undriven_104),
    .RRXout(undriven_105), .in_1(DATAin), .clock(clock), .reset(reset), .out_14(DATAout));
  block_reg_sizes RBP (
    .RLin(undriven_26), .RHin(undriven_27), .RXin(undriven_28), .ERXin(undriven_29), .RRXin(undriven_30),
    .RLout(undriven_106), .RHout(undriven_107), .RXout(undriven_108), .ERXout(undriven_109),
    .RRXout(undriven_110), .in_1(DATAin), .clock(clock), .reset(reset), .out_14(DATAout));
  block_reg_sizes RSI (
    .RLin(undriven_31), .RHin(undriven_32), .RXin(undriven_33), .ERXin(undriven_34), .RRXin(undriven_35),
    .RLout(undriven_111), .RHout(undriven_112), .RXout(undriven_113), .ERXout(undriven_114),
    .RRXout(undriven_115), .in_1(DATAin), .clock(clock), .reset(reset), .out_14(DATAout));
  block_reg_sizes RDI (
    .RLin(undriven_36), .RHin(undriven_37), .RXin(undriven_38), .ERXin(undriven_39), .RRXin(undriven_40),
    .RLout(undriven_116), .RHout(undriven_117), .RXout(undriven_118), .ERXout(undriven_119),
    .RRXout(undriven_120), .in_1(DATAin), .clock(clock), .reset(reset), .out_14(DATAout));
  block_reg_sizes R8 (
    .RLin(undriven_41), .RHin(undriven_42), .RXin(undriven_43), .ERXin(undriven_44), .RRXin(undriven_45),
    .RLout(undriven_121), .RHout(undriven_122), .RXout(undriven_123), .ERXout(undriven_124),
    .RRXout(undriven_125), .in_1(DATAin), .clock(clock), .reset(reset), .out_14(DATAout));
  block_reg_sizes R9 (
    .RLin(undriven_46), .RHin(undriven_47), .RXin(undriven_48), .ERXin(undriven_49), .RRXin(undriven_50),
    .RLout(undriven_126), .RHout(undriven_127), .RXout(undriven_128), .ERXout(undriven_129),
    .RRXout(undriven_130), .in_1(DATAin), .clock(clock), .reset(reset), .out_14(DATAout));
  block_reg_sizes R10 (
    .RLin(undriven_51), .RHin(undriven_52), .RXin(undriven_53), .ERXin(undriven_54), .RRXin(undriven_55),
    .RLout(undriven_131), .RHout(undriven_132), .RXout(undriven_133), .ERXout(undriven_134),
    .RRXout(undriven_135), .in_1(DATAin), .clock(clock), .reset(reset), .out_14(DATAout));
  block_reg_sizes R11 (
    .RLin(undriven_56), .RHin(undriven_57), .RXin(undriven_58), .ERXin(undriven_59), .RRXin(undriven_60),
    .RLout(undriven_136), .RHout(undriven_137), .RXout(undriven_138), .ERXout(undriven_139),
    .RRXout(undriven_140), .in_1(DATAin), .clock(clock), .reset(reset), .out_14(DATAout));
  block_reg_sizes R12 (
    .RLin(undriven_61), .RHin(undriven_62), .RXin(undriven_63), .ERXin(undriven_64), .RRXin(undriven_65),
    .RLout(undriven_141), .RHout(undriven_142), .RXout(undriven_143), .ERXout(undriven_144),
    .RRXout(undriven_145), .in_1(DATAin), .clock(clock), .reset(reset), .out_14(DATAout));
  block_reg_sizes R13 (
    .RLin(undriven_66), .RHin(undriven_67), .RXin(undriven_68), .ERXin(undriven_69), .RRXin(undriven_70),
    .RLout(undriven_146), .RHout(undriven_147), .RXout(undriven_148), .ERXout(undriven_149),
    .RRXout(undriven_150), .in_1(DATAin), .clock(clock), .reset(reset), .out_14(DATAout));
  block_reg_sizes R14 (
    .RLin(undriven_71), .RHin(undriven_72), .RXin(undriven_73), .ERXin(undriven_74), .RRXin(undriven_75),
    .RLout(undriven_151), .RHout(undriven_152), .RXout(undriven_153), .ERXout(undriven_154),
    .RRXout(undriven_155), .in_1(DATAin), .clock(clock), .reset(reset), .out_14(DATAout));
  block_reg_sizes R15 (
    .RLin(undriven_76), .RHin(undriven_77), .RXin(undriven_78), .ERXin(undriven_79), .RRXin(undriven_80),
    .RLout(undriven_156), .RHout(undriven_157), .RXout(undriven_158), .ERXout(undriven_159),
    .RRXout(undriven_160), .in_1(DATAin), .clock(clock), .reset(reset), .out_14(DATAout));
endmodule

module block_reg_sizes (
  input  [63:0] in_1,
  input  RLin,
  input  RHin,
  input  RXin,
  input  ERXin,
  input  RRXin,
  input  RLout,
  input  RHout,
  input  RXout,
  input  ERXout,
  input  RRXout,
  input  clock,
  input  reset,
  output [63:0] out_14
);

  wire or_1_out, or_2_out, or_3_out, or_4_out, or_5_out, or_6_out;
  wire [7:0] register_1_q, register_2_q;
  wire [15:0] register_3_q;
  wire [31:0] register_4_q;

  or or_1 (or_1_out, RLin, RXin, ERXin, RRXin);
  or or_2 (or_2_out, RHin, RXin, ERXin, RRXin);
  or or_3 (or_3_out, ERXin, RRXin);
  or or_4 (or_4_out, RLout, RXout, ERXout, RRXout);
  or or_5 (or_5_out, RHout, RXout, ERXout, RRXout);
  or or_6 (or_6_out, ERXout, RRXout);
  LED led_1 (.in(or_1_out));
  LED led_2 (.in(or_2_out));
  LED led_3 (.in(or_3_out));
  LED led_4 (.in(RRXin));
  LED led_5 (.in(or_4_out));
  LED led_6 (.in(or_5_out));
  LED led_7 (.in(or_6_out));
  LED led_8 (.in(RRXout));
  Register register_1 (.D(in_1[7:0]), .en(or_1_out), .clk(clock), .Q(register_1_q), .clr(reset));
  Register register_2 (.D(in_1[15:8]), .en(or_2_out), .clk(clock), .Q(register_2_q), .clr(reset));
  Register #(.width(16)) register_3 (.D(in_1[31:16]), .en(or_3_out), .clk(clock), .Q(register_3_q), .clr(reset));
  Register #(.width(32)) register_4 (.D(in_1[63:32]), .en(RRXin), .clk(clock), .Q(register_4_q), .clr(reset));
  assign out_14[7:0] = or_4_out ? register_1_q : 8'bz;  // Controlled_Buffer controlled_buffer_1
  assign out_14[15:8] = or_5_out ? register_2_q : 8'bz;  // Controlled_Buffer controlled_buffer_2
  assign out_14[31:16] = or_6_out ? register_3_q : 16'bz;  // Controlled_Buffer controlled_buffer_3
  assign out_14[63:32] = RRXout ? register_4_q : 32'bz;  // Controlled_Buffer controlled_buffer_4
endmodule

module block_ALU (
  input  [63:0] DATAin,
  input  YREGin,
  input  ZREGin,
  input  clock,
  input  reset,
  input  Select4,
  input  SelectY,
  input  SETC,
  input  CLC,
  input  CMC,
  input  [4:0] aluOPCODE,
  input  enableALU,
  output [63:0] DATAout
);

  wire block_alu_operation_bus_1_enablealuout, block_alu_operation_bus_1_enablealuout_1,
       block_alu_operation_bus_1_enablealuout_2, block_alu_operation_bus_1_enablealuout_3, or_1_out;
  wire [4:0] block_alu_operation_bus_1_aluopcodeout, block_alu_operation_bus_1_aluopcodeout_1,
       block_alu_operation_bus_1_aluopcodeout_2, block_alu_operation_bus_1_aluopcodeout_3;
  wire [63:0] block_alu_flag_register_1_dataout, block_alu_group1_core_arithmetic_1_rflagsout,
       block_alu_group1_core_arithmetic_1_zout, block_alu_operation_bus_1_dataouta,
       block_alu_operation_bus_1_dataouta_1, block_alu_operation_bus_1_dataouta_2,
       block_alu_operation_bus_1_dataouta_3, block_alu_operation_bus_1_operandbout,
       block_alu_operation_bus_1_operandbout_1, block_alu_operation_bus_1_operandbout_2,
       block_alu_operation_bus_1_operandbout_3, block_alu_operation_bus_1_rflagsout,
       block_alu_operation_bus_1_rflagsout_1, block_alu_operation_bus_1_rflagsout_2,
       block_alu_operation_bus_1_rflagsout_3, multiplexer_1_out, YREG_q;

  Register #(.width(64)) YREG (.D(DATAin), .en(YREGin), .clk(clock), .Q(YREG_q), .clr(reset));
  block_ALU_flag_register block_alu_flag_register_1 (
    .DATAin(block_alu_group1_core_arithmetic_1_rflagsout), .CMC(CMC), .CLC(CLC), .SETC(SETC), .clock(clock),
    .Reset(reset), .DATAout(block_alu_flag_register_1_dataout));
  Multiplexer #(.enable("true"), .width(64)) multiplexer_1 (
    .in0(YREG_q), .in1(64'h4), .out(multiplexer_1_out), .sel(Select4), .en(or_1_out));
  or or_1 (or_1_out, Select4, SelectY);
  block_ALU_operation_bus block_alu_operation_bus_1 (
    .CLOCK(clock), .RESET(reset), .RFLAGin(block_alu_flag_register_1_dataout),
    .OPERANDBin(multiplexer_1_out), .DATAinA(DATAin), .aluOPCODE(aluOPCODE), .enableALU(enableALU),
    .RFLAGSout_3(block_alu_operation_bus_1_rflagsout_3),
    .OPERANDBout_3(block_alu_operation_bus_1_operandbout_3),
    .DATAoutA_3(block_alu_operation_bus_1_dataouta_3),
    .aluOPCODEout_3(block_alu_operation_bus_1_aluopcodeout_3),
    .enableALUout_3(block_alu_operation_bus_1_enablealuout_3),
    .RFLAGSout(block_alu_operation_bus_1_rflagsout), .OPERANDBout(block_alu_operation_bus_1_operandbout),
    .DATAoutA(block_alu_operation_bus_1_dataouta), .aluOPCODEout(block_alu_operation_bus_1_aluopcodeout),
    .enableALUout(block_alu_operation_bus_1_enablealuout),
    .RFLAGSout_1(block_alu_operation_bus_1_rflagsout_1),
    .OPERANDBout_1(block_alu_operation_bus_1_operandbout_1),
    .DATAoutA_1(block_alu_operation_bus_1_dataouta_1),
    .aluOPCODEout_1(block_alu_operation_bus_1_aluopcodeout_1),
    .enableALUout_1(block_alu_operation_bus_1_enablealuout_1),
    .RFLAGSout_2(block_alu_operation_bus_1_rflagsout_2),
    .OPERANDBout_2(block_alu_operation_bus_1_operandbout_2),
    .DATAoutA_2(block_alu_operation_bus_1_dataouta_2),
    .aluOPCODEout_2(block_alu_operation_bus_1_aluopcodeout_2),
    .enableALUout_2(block_alu_operation_bus_1_enablealuout_2));
  block_ALU_group1_core_arithmetic block_alu_group1_core_arithmetic_1 (
    .enableG1(block_alu_operation_bus_1_enablealuout), .opcode(block_alu_operation_bus_1_aluopcodeout),
    .RFLAGSin(block_alu_operation_bus_1_rflagsout), .Bin(block_alu_operation_bus_1_operandbout),
    .Ain(block_alu_operation_bus_1_dataouta), .Zout(block_alu_group1_core_arithmetic_1_zout),
    .RFLAGSout(block_alu_group1_core_arithmetic_1_rflagsout));
  block_ALU_group3_unary_mul_div block_alu_group3_unary_mul_div_1 (
    .enableG3(block_alu_operation_bus_1_enablealuout_1), .opcode(block_alu_operation_bus_1_aluopcodeout_1),
    .RFLAGSin(block_alu_operation_bus_1_rflagsout_1), .Bin(block_alu_operation_bus_1_dataouta_1),
    .Ain(block_alu_operation_bus_1_operandbout_1), .Zout(block_alu_group1_core_arithmetic_1_zout),
    .RFLAGSout(block_alu_group1_core_arithmetic_1_rflagsout));
  block_ALU_group5 block_alu_group5_1 (
    .enableG5(block_alu_operation_bus_1_enablealuout_2), .opcode(block_alu_operation_bus_1_aluopcodeout_2),
    .RFLAGSin(block_alu_operation_bus_1_rflagsout_2), .Bin(block_alu_operation_bus_1_dataouta_2),
    .Ain(block_alu_operation_bus_1_operandbout_2), .Zout(block_alu_group1_core_arithmetic_1_zout),
    .RFLAGSout(block_alu_group1_core_arithmetic_1_rflagsout));
  block_ALU_group8_bit_test_modify block_alu_group8_bit_test_modify_1 (
    .enableG8(block_alu_operation_bus_1_enablealuout_3), .opcode(block_alu_operation_bus_1_aluopcodeout_3),
    .RFLAGSin(block_alu_operation_bus_1_rflagsout_3), .Bin(block_alu_operation_bus_1_dataouta_3),
    .Ain(block_alu_operation_bus_1_operandbout_3), .Zout(block_alu_group1_core_arithmetic_1_zout),
    .RFLAGSout(block_alu_group1_core_arithmetic_1_rflagsout));
  Register #(.width(64)) ZREG (
    .D(block_alu_group1_core_arithmetic_1_zout), .en(ZREGin), .clk(clock), .Q(DATAout), .clr(reset));
endmodule

module block_ALU_operation_bus (
  input  CLOCK,
  input  RESET,
  input  [63:0] RFLAGin,
  input  [63:0] OPERANDBin,
  input  [63:0] DATAinA,
  input  [4:0] aluOPCODE,
  input  enableALU,
  output [63:0] RFLAGSout,
  output [63:0] OPERANDBout,
  output [63:0] DATAoutA,
  output [4:0] aluOPCODEout,
  output enableALUout,
  output [63:0] RFLAGSout_1,
  output [63:0] OPERANDBout_1,
  output [63:0] DATAoutA_1,
  output [4:0] aluOPCODEout_1,
  output enableALUout_1,
  output [63:0] RFLAGSout_2,
  output [63:0] OPERANDBout_2,
  output [63:0] DATAoutA_2,
  output [4:0] aluOPCODEout_2,
  output enableALUout_2,
  output [63:0] RFLAGSout_3,
  output [63:0] OPERANDBout_3,
  output [63:0] DATAoutA_3,
  output [4:0] aluOPCODEout_3,
  output enableALUout_3
);

  LED signALU (.in(enableALU));
  Register #(.width(64)) signDATAinA (.D(DATAinA), .clk(CLOCK), .clr(RESET));  // open: en, Q
  Register #(.width(5)) signOPCODE (.D(aluOPCODE), .clk(CLOCK), .clr(RESET));  // open: en, Q

  assign aluOPCODEout = aluOPCODE;
  assign aluOPCODEout_1 = aluOPCODE;
  assign aluOPCODEout_2 = aluOPCODE;
  assign aluOPCODEout_3 = aluOPCODE;
  assign DATAoutA = DATAinA;
  assign DATAoutA_1 = DATAinA;
  assign DATAoutA_2 = DATAinA;
  assign DATAoutA_3 = DATAinA;
  assign enableALUout = enableALU;
  assign enableALUout_1 = enableALU;
  assign enableALUout_2 = enableALU;
  assign enableALUout_3 = enableALU;
  assign OPERANDBout = OPERANDBin;
  assign OPERANDBout_1 = OPERANDBin;
  assign OPERANDBout_2 = OPERANDBin;
  assign OPERANDBout_3 = OPERANDBin;
  assign RFLAGSout = RFLAGin;
  assign RFLAGSout_1 = RFLAGin;
  assign RFLAGSout_2 = RFLAGin;
  assign RFLAGSout_3 = RFLAGin;
endmodule

module block_ALU_group1_core_arithmetic (
  input  [4:0] opcode,
  input  enableG1,
  input  [63:0] RFLAGSin,
  input  [63:0] Bin,
  input  [63:0] Ain,
  output [63:0] Zout,
  output [63:0] RFLAGSout
);

  wire adder_1_cout, adder_2_cout, comparator_1_eq, comparator_1_lt, subtractor_1_bout, subtractor_2_bout;
  wire [63:0] adder_1_out, adder_2_out, and_1_out, block_alu_flag_detection_1_rflagsout,
       block_alu_flag_detection_2_rflagsout, block_alu_flag_detection_3_rflagsout,
       block_alu_flag_detection_4_rflagsout, block_alu_flag_detection_5_rflagsout,
       block_alu_flag_detection_6_rflagsout, block_alu_flag_detection_7_rflagsout,
       block_alu_flag_detection_8_rflagsout, or_1_out, subtractor_1_out, subtractor_2_out, undriven,
       xor_1_out;

  Adder #(.width(64)) adder_1 (.a(Ain), .b(Bin), .out(adder_1_out), .cin(1'b0), .cout(adder_1_cout));
  assign or_1_out = Ain | Bin;  // OR_Gate or_1, 64 bits wide
  Adder #(.width(64)) adder_2 (.a(Ain), .b(Bin), .out(adder_2_out), .cin(RFLAGSin[0]), .cout(adder_2_cout));
  Subtractor #(.width(64)) subtractor_1 (
    .a(Ain), .b(Bin), .out(subtractor_1_out), .bin(RFLAGSin[0]), .bout(subtractor_1_bout));
  assign and_1_out = Ain & Bin;  // AND_Gate and_1, 64 bits wide
  Subtractor #(.width(64)) subtractor_2 (
    .a(Ain), .b(Bin), .out(subtractor_2_out), .bin(1'b0), .bout(subtractor_2_bout));
  assign xor_1_out = Ain ^ Bin;  // XOR_Gate xor_1, 64 bits wide
  Comparator #(.width(64)) comparator_1 (.a(Ain), .b(Bin), .eq(comparator_1_eq), .lt(comparator_1_lt));  // open: gt
  Multiplexer #(.disabled("Z"), .enable("true"), .select(5), .width(64)) multiplexer_1 (
    .in0(adder_1_out), .in1(or_1_out), .in2(adder_2_out), .in3(subtractor_1_out), .in4(and_1_out),
    .in5(undriven), .in6(xor_1_out), .out(Zout), .sel(opcode), .en(enableG1));  // open: in7, in8, in9, in10, in11, in12, in13, in14, in15, in16, in17, in18, in19, in20, in21, in22, in23, in24, in25, in26, in27, in28, in29, in30, in31
  block_ALU_flag_detection block_alu_flag_detection_1 (
    .RFLAGSin(RFLAGSin), .DATAin(adder_1_out), .SIGNgenerate(1'b1), .OVERFLOWgenerate(1'b1),
    .CARRYin(adder_1_cout), .CARRYset(1'b1), .PARITYgenerate(1'b1), .ZEROgenerate(1'b1),
    .RFLAGSout(block_alu_flag_detection_1_rflagsout));  // open: OVERFLOWin, OVERFLOWset, PARITYin, PARITYset, AUXin, AUXset, ZEROin, ZEROset, SIGNin, SIGNset
  block_ALU_flag_detection block_alu_flag_detection_2 (
    .RFLAGSin(RFLAGSin), .DATAin(or_1_out), .SIGNgenerate(1'b1), .OVERFLOWin(1'b0), .OVERFLOWset(1'b1),
    .CARRYin(1'b0), .CARRYset(1'b1), .PARITYgenerate(1'b1), .ZEROgenerate(1'b1),
    .RFLAGSout(block_alu_flag_detection_2_rflagsout));  // open: OVERFLOWgenerate, PARITYin, PARITYset, AUXin, AUXset, ZEROin, ZEROset, SIGNin, SIGNset
  block_ALU_flag_detection block_alu_flag_detection_3 (
    .RFLAGSin(RFLAGSin), .DATAin(adder_2_out), .SIGNgenerate(1'b1), .OVERFLOWgenerate(1'b1),
    .CARRYin(adder_2_cout), .CARRYset(1'b1), .PARITYgenerate(1'b1), .ZEROgenerate(1'b1),
    .RFLAGSout(block_alu_flag_detection_3_rflagsout));  // open: OVERFLOWin, OVERFLOWset, PARITYin, PARITYset, AUXin, AUXset, ZEROin, ZEROset, SIGNin, SIGNset
  block_ALU_flag_detection block_alu_flag_detection_4 (
    .RFLAGSin(RFLAGSin), .DATAin(subtractor_1_out), .SIGNgenerate(1'b1), .OVERFLOWgenerate(1'b1),
    .CARRYin(subtractor_1_bout), .CARRYset(1'b1), .PARITYgenerate(1'b1), .ZEROgenerate(1'b1),
    .RFLAGSout(block_alu_flag_detection_4_rflagsout));  // open: OVERFLOWin, OVERFLOWset, PARITYin, PARITYset, AUXin, AUXset, ZEROin, ZEROset, SIGNin, SIGNset
  block_ALU_flag_detection block_alu_flag_detection_5 (
    .RFLAGSin(RFLAGSin), .DATAin(and_1_out), .SIGNgenerate(1'b1), .OVERFLOWin(1'b0), .OVERFLOWset(1'b1),
    .CARRYin(1'b0), .CARRYset(1'b1), .PARITYgenerate(1'b1), .ZEROgenerate(1'b1),
    .RFLAGSout(block_alu_flag_detection_5_rflagsout));  // open: OVERFLOWgenerate, PARITYin, PARITYset, AUXin, AUXset, ZEROin, ZEROset, SIGNin, SIGNset
  block_ALU_flag_detection block_alu_flag_detection_6 (
    .RFLAGSin(RFLAGSin), .DATAin(subtractor_2_out), .SIGNgenerate(1'b1), .OVERFLOWgenerate(1'b1),
    .CARRYin(subtractor_2_bout), .CARRYset(1'b1), .PARITYgenerate(1'b1), .ZEROgenerate(1'b1),
    .RFLAGSout(block_alu_flag_detection_6_rflagsout));  // open: OVERFLOWin, OVERFLOWset, PARITYin, PARITYset, AUXin, AUXset, ZEROin, ZEROset, SIGNin, SIGNset
  block_ALU_flag_detection block_alu_flag_detection_7 (
    .RFLAGSin(RFLAGSin), .DATAin(xor_1_out), .SIGNgenerate(1'b1), .OVERFLOWin(1'b0), .OVERFLOWset(1'b1),
    .CARRYin(1'b0), .CARRYset(1'b1), .PARITYgenerate(1'b1), .ZEROgenerate(1'b1),
    .RFLAGSout(block_alu_flag_detection_7_rflagsout));  // open: OVERFLOWgenerate, PARITYin, PARITYset, AUXin, AUXset, ZEROin, ZEROset, SIGNin, SIGNset
  block_ALU_flag_detection block_alu_flag_detection_8 (
    .RFLAGSin(RFLAGSin), .OVERFLOWgenerate(1'b1), .PARITYgenerate(1'b1), .ZEROin(comparator_1_eq),
    .ZEROset(1'b1), .SIGNin(comparator_1_lt), .RFLAGSout(block_alu_flag_detection_8_rflagsout));  // open: DATAin, SIGNgenerate, OVERFLOWin, OVERFLOWset, CARRYin, CARRYset, PARITYin, PARITYset, AUXin, AUXset, ZEROgenerate, SIGNset
  Pull_Resistor pull_resistor_1 (.node(RFLAGSout));
  Multiplexer #(.disabled("Z"), .enable("true"), .select(5), .width(64)) multiplexer_2 (
    .in0(block_alu_flag_detection_1_rflagsout), .in1(block_alu_flag_detection_2_rflagsout),
    .in2(block_alu_flag_detection_3_rflagsout), .in3(block_alu_flag_detection_4_rflagsout),
    .in4(block_alu_flag_detection_5_rflagsout), .in5(block_alu_flag_detection_6_rflagsout),
    .in6(block_alu_flag_detection_7_rflagsout), .in7(block_alu_flag_detection_8_rflagsout), .out(RFLAGSout),
    .sel(opcode), .en(enableG1));  // open: in8, in9, in10, in11, in12, in13, in14, in15, in16, in17, in18, in19, in20, in21, in22, in23, in24, in25, in26, in27, in28, in29, in30, in31
endmodule

module block_ALU_group3_unary_mul_div (
  input  [4:0] opcode,
  input  enableG3,
  input  [63:0] RFLAGSin,
  input  [63:0] Bin,
  input  [63:0] Ain,
  output [63:0] Zout,
  output [63:0] RFLAGSout
);

  wire block_alu_flag_detection_1_p3, undriven, undriven_2, undriven_3;
  wire [63:0] block_alu_flag_detection_1_p6, block_alu_flag_detection_2_rflagsout,
       block_alu_flag_detection_3_rflagsout, block_alu_flag_detection_4_rflagsout,
       block_alu_flag_detection_5_rflagsout, block_alu_flag_detection_6_rflagsout, divider_1_out,
       divider_2_out, multiplier_1_out, multiplier_2_out, negator_1_out, not_1_out;

  assign not_1_out = ~Ain;  // NOT_Gate not_1, 64 bits wide
  Negator #(.width(64)) negator_1 (.in(Ain), .out(negator_1_out));
  Multiplier #(.width(64)) multiplier_1 (.a(Ain), .b(Bin), .out(multiplier_1_out));  // open: cin, cout
  Multiplier #(.mode("twosComplement"), .width(64)) multiplier_2 (
    .a(Ain), .b(Bin), .out(multiplier_2_out));  // open: cin, cout
  Divider #(.width(64)) divider_1 (.a(Ain), .b(Bin), .out(divider_1_out));  // open: upper, rem
  Divider #(.mode("twosComplement"), .width(64)) divider_2 (.a(Ain), .b(Bin), .out(divider_2_out));  // open: upper, rem
  Multiplexer #(.disabled("Z"), .enable("true"), .select(5), .width(64)) multiplexer_1 (
    .in15(not_1_out), .in16(negator_1_out), .in17(multiplier_1_out), .in18(multiplier_2_out),
    .in19(divider_1_out), .in20(divider_2_out), .out(Zout), .sel(opcode), .en(enableG3));  // open: in0, in1, in2, in3, in4, in5, in6, in7, in8, in9, in10, in11, in12, in13, in14, in21, in22, in23, in24, in25, in26, in27, in28, in29, in30, in31
  // block_ALU_flag_detection block_alu_flag_detection_1: pin names not known; wires that end beside it: not_1_out, RFLAGSin, block_alu_flag_detection_1_p3, block_alu_flag_detection_1_p3, 1'b1, block_alu_flag_detection_1_p6
  block_ALU_flag_detection block_alu_flag_detection_2 (
    .RFLAGSin(RFLAGSin), .DATAin(negator_1_out), .SIGNgenerate(1'b1), .OVERFLOWgenerate(1'b1),
    .CARRYset(1'b0), .PARITYgenerate(1'b1), .ZEROgenerate(1'b1),
    .RFLAGSout(block_alu_flag_detection_2_rflagsout));  // open: OVERFLOWin, OVERFLOWset, CARRYin, PARITYin, PARITYset, AUXin, AUXset, ZEROin, ZEROset, SIGNin, SIGNset
  block_ALU_flag_detection block_alu_flag_detection_3 (
    .RFLAGSin(RFLAGSin), .DATAin(multiplier_1_out), .SIGNgenerate(1'b1), .OVERFLOWgenerate(1'b1),
    .CARRYin(undriven), .CARRYset(1'b1), .PARITYgenerate(1'b1), .ZEROgenerate(1'b1),
    .RFLAGSout(block_alu_flag_detection_3_rflagsout));  // open: OVERFLOWin, OVERFLOWset, PARITYin, PARITYset, AUXin, AUXset, ZEROin, ZEROset, SIGNin, SIGNset
  block_ALU_flag_detection block_alu_flag_detection_4 (
    .RFLAGSin(RFLAGSin), .DATAin(multiplier_2_out), .SIGNgenerate(1'b1), .OVERFLOWgenerate(1'b1),
    .CARRYin(undriven_2), .CARRYset(1'b1), .PARITYgenerate(1'b1), .ZEROgenerate(1'b1),
    .RFLAGSout(block_alu_flag_detection_4_rflagsout));  // open: OVERFLOWin, OVERFLOWset, PARITYin, PARITYset, AUXin, AUXset, ZEROin, ZEROset, SIGNin, SIGNset
  block_ALU_flag_detection block_alu_flag_detection_5 (
    .RFLAGSin(RFLAGSin), .DATAin(divider_1_out), .SIGNgenerate(1'b1), .OVERFLOWgenerate(1'b1),
    .CARRYset(1'b1), .PARITYgenerate(1'b1), .ZEROgenerate(1'b1),
    .RFLAGSout(block_alu_flag_detection_5_rflagsout));  // open: OVERFLOWin, OVERFLOWset, CARRYin, PARITYin, PARITYset, AUXin, AUXset, ZEROin, ZEROset, SIGNin, SIGNset
  block_ALU_flag_detection block_alu_flag_detection_6 (
    .RFLAGSin(RFLAGSin), .DATAin(divider_2_out), .SIGNgenerate(1'b1), .OVERFLOWgenerate(1'b1),
    .CARRYin(undriven_3), .CARRYset(1'b1), .PARITYgenerate(1'b1), .ZEROgenerate(1'b1),
    .RFLAGSout(block_alu_flag_detection_6_rflagsout));  // open: OVERFLOWin, OVERFLOWset, PARITYin, PARITYset, AUXin, AUXset, ZEROin, ZEROset, SIGNin, SIGNset
  Pull_Resistor pull_resistor_1 (.node(RFLAGSout));
  Multiplexer #(.disabled("Z"), .enable("true"), .select(5), .width(64)) multiplexer_2 (
    .in15(block_alu_flag_detection_1_p6), .in16(block_alu_flag_detection_2_rflagsout),
    .in17(block_alu_flag_detection_3_rflagsout), .in18(block_alu_flag_detection_4_rflagsout),
    .in19(block_alu_flag_detection_5_rflagsout), .in20(block_alu_flag_detection_6_rflagsout),
    .out(RFLAGSout), .sel(opcode), .en(enableG3));  // open: in0, in1, in2, in3, in4, in5, in6, in7, in8, in9, in10, in11, in12, in13, in14, in21, in22, in23, in24, in25, in26, in27, in28, in29, in30, in31
endmodule

module block_ALU_group5 (
  input  [4:0] opcode,
  input  enableG5,
  input  [63:0] RFLAGSin,
  input  [63:0] Bin,
  input  [63:0] Ain,
  output [63:0] Zout,
  output [63:0] RFLAGSout
);

  wire [63:0] adder_1_out, block_alu_flag_detection_1_rflagsout, block_alu_flag_detection_2_rflagsout,
       subtractor_1_out;

  Adder #(.width(64)) adder_1 (.a(Ain), .b({64{1'b0}}), .out(adder_1_out), .cin(1'b1));  // open: cout
  Subtractor #(.width(64)) subtractor_1 (.a(Ain), .b({64{1'b0}}), .out(subtractor_1_out), .bin(1'b1));  // open: bout
  Multiplexer #(.disabled("Z"), .enable("true"), .select(5), .width(64)) multiplexer_1 (
    .in21(adder_1_out), .in22(subtractor_1_out), .out(Zout), .sel(opcode), .en(enableG5));  // open: in0, in1, in2, in3, in4, in5, in6, in7, in8, in9, in10, in11, in12, in13, in14, in15, in16, in17, in18, in19, in20, in23, in24, in25, in26, in27, in28, in29, in30, in31
  block_ALU_flag_detection block_alu_flag_detection_1 (
    .RFLAGSin(RFLAGSin), .DATAin(adder_1_out), .SIGNgenerate(1'b1), .OVERFLOWgenerate(1'b1), .CARRYset(1'b0),
    .PARITYgenerate(1'b1), .ZEROgenerate(1'b1), .RFLAGSout(block_alu_flag_detection_1_rflagsout));  // open: OVERFLOWin, OVERFLOWset, CARRYin, PARITYin, PARITYset, AUXin, AUXset, ZEROin, ZEROset, SIGNin, SIGNset
  block_ALU_flag_detection block_alu_flag_detection_2 (
    .RFLAGSin(RFLAGSin), .DATAin(subtractor_1_out), .SIGNgenerate(1'b1), .OVERFLOWgenerate(1'b1),
    .CARRYset(1'b0), .PARITYgenerate(1'b1), .ZEROgenerate(1'b1),
    .RFLAGSout(block_alu_flag_detection_2_rflagsout));  // open: OVERFLOWin, OVERFLOWset, CARRYin, PARITYin, PARITYset, AUXin, AUXset, ZEROin, ZEROset, SIGNin, SIGNset
  Pull_Resistor pull_resistor_1 (.node(RFLAGSout));
  Multiplexer #(.disabled("Z"), .enable("true"), .select(5), .width(64)) multiplexer_2 (
    .in21(block_alu_flag_detection_1_rflagsout), .in22(block_alu_flag_detection_2_rflagsout),
    .out(RFLAGSout), .sel(opcode), .en(enableG5));  // open: in0, in1, in2, in3, in4, in5, in6, in7, in8, in9, in10, in11, in12, in13, in14, in15, in16, in17, in18, in19, in20, in23, in24, in25, in26, in27, in28, in29, in30, in31
endmodule

module block_ALU_group8_bit_test_modify (
  input  [4:0] opcode,
  input  enableG8,
  input  [63:0] RFLAGSin,
  input  [63:0] Bin,
  input  [63:0] Ain,
  output [63:0] Zout,
  output [63:0] RFLAGSout
);

  wire [63:0] and_1_out, block_alu_flag_detection_1_rflagsout;

  assign and_1_out = Ain & Bin;  // AND_Gate and_1, 64 bits wide
  Multiplexer #(.disabled("Z"), .enable("true"), .select(5), .width(64)) multiplexer_1 (
    .in23(and_1_out), .out(Zout), .sel(opcode), .en(enableG8));  // open: in0, in1, in2, in3, in4, in5, in6, in7, in8, in9, in10, in11, in12, in13, in14, in15, in16, in17, in18, in19, in20, in21, in22, in24, in25, in26, in27, in28, in29, in30, in31
  block_ALU_flag_detection block_alu_flag_detection_1 (
    .RFLAGSin(RFLAGSin), .DATAin(and_1_out), .SIGNgenerate(1'b1), .OVERFLOWin(1'b0), .OVERFLOWset(1'b1),
    .CARRYin(1'b0), .CARRYset(1'b1), .PARITYgenerate(1'b1), .ZEROgenerate(1'b1),
    .RFLAGSout(block_alu_flag_detection_1_rflagsout));  // open: OVERFLOWgenerate, PARITYin, PARITYset, AUXin, AUXset, ZEROin, ZEROset, SIGNin, SIGNset
  Pull_Resistor pull_resistor_1 (.node(RFLAGSout));
  Multiplexer #(.disabled("Z"), .enable("true"), .select(5), .width(64)) multiplexer_2 (
    .in23(block_alu_flag_detection_1_rflagsout), .out(RFLAGSout), .sel(opcode), .en(enableG8));  // open: in0, in1, in2, in3, in4, in5, in6, in7, in8, in9, in10, in11, in12, in13, in14, in15, in16, in17, in18, in19, in20, in21, in22, in24, in25, in26, in27, in28, in29, in30, in31
endmodule

module block_ALU_flag_detection (
  input  [63:0] RFLAGSin,
  input  [63:0] DATAin,
  input  CARRYin,
  input  CARRYset,
  input  PARITYin,
  input  PARITYset,
  input  PARITYgenerate,
  input  AUXin,
  input  AUXset,
  input  ZEROin,
  input  ZEROset,
  input  ZEROgenerate,
  input  SIGNin,
  input  SIGNset,
  input  SIGNgenerate,
  input  OVERFLOWin,
  input  OVERFLOWset,
  input  OVERFLOWgenerate,
  output [63:0] RFLAGSout
);

  wire multiplexer_2_out, multiplexer_4_out, multiplexer_5_out, multiplexer_6_out, nor_1_out, xor_1_out,
       xor_2_out;

  xor xor_1 (xor_1_out, DATAin[63], DATAin[63]);
  nor nor_1 (nor_1_out, DATAin[63], DATAin[62], DATAin[61], DATAin[60], DATAin[59], DATAin[58], DATAin[57], DATAin[56], DATAin[55], DATAin[54], DATAin[53], DATAin[52], DATAin[51], DATAin[50], DATAin[49], DATAin[48], DATAin[47], DATAin[46], DATAin[45], DATAin[44], DATAin[43], DATAin[42], DATAin[41], DATAin[40], DATAin[39], DATAin[38], DATAin[37], DATAin[36], DATAin[35], DATAin[34], DATAin[33], DATAin[32], DATAin[31], DATAin[30], DATAin[29], DATAin[28], DATAin[27], DATAin[26], DATAin[25], DATAin[24], DATAin[23], DATAin[22], DATAin[21], DATAin[20], DATAin[19], DATAin[18], DATAin[17], DATAin[16], DATAin[15], DATAin[14], DATAin[13], DATAin[12], DATAin[11], DATAin[10], DATAin[9], DATAin[8], DATAin[7], DATAin[6], DATAin[5], DATAin[4], DATAin[3], DATAin[2], DATAin[1], DATAin[0]);
  Multiplexer multiplexer_1 (.in0(RFLAGSin[0]), .in1(CARRYin), .out(RFLAGSout[0]), .sel(CARRYset));
  Multiplexer multiplexer_2 (.in0(RFLAGSin[2]), .in1(PARITYin), .out(multiplexer_2_out), .sel(PARITYset));
  Multiplexer multiplexer_3 (.in0(RFLAGSin[4]), .in1(AUXin), .out(RFLAGSout[4]), .sel(AUXset));
  Multiplexer multiplexer_4 (.in0(RFLAGSin[6]), .in1(ZEROin), .out(multiplexer_4_out), .sel(ZEROset));
  Multiplexer multiplexer_5 (.in0(RFLAGSin[7]), .in1(SIGNin), .out(multiplexer_5_out), .sel(SIGNset));
  Multiplexer multiplexer_6 (.in0(RFLAGSin[8]), .in1(OVERFLOWin), .out(multiplexer_6_out), .sel(OVERFLOWset));
  Multiplexer multiplexer_7 (.in0(multiplexer_2_out), .in1(xor_2_out), .out(RFLAGSout[2]), .sel(PARITYgenerate));
  Multiplexer multiplexer_8 (.in0(multiplexer_4_out), .in1(DATAin[63]), .out(RFLAGSout[6]), .sel(ZEROgenerate));
  Multiplexer multiplexer_9 (.in0(multiplexer_5_out), .in1(nor_1_out), .out(RFLAGSout[7]), .sel(SIGNgenerate));
  Multiplexer multiplexer_10 (.in0(multiplexer_6_out), .in1(xor_1_out), .out(RFLAGSout[8]), .sel(OVERFLOWgenerate));
  ExactlyOne xor_2 (
    .out(xor_2_out), .in0(DATAin[7]), .in1(DATAin[6]), .in2(DATAin[5]), .in3(DATAin[4]), .in4(DATAin[3]),
    .in5(DATAin[2]), .in6(DATAin[1]), .in7(DATAin[0]));

  assign {RFLAGSout[63:9], RFLAGSout[5], RFLAGSout[3], RFLAGSout[1]} = {RFLAGSin[63:9], RFLAGSin[5], RFLAGSin[3], RFLAGSin[1]};
endmodule

module block_ALU_flag_register (
  input  [63:0] DATAin,
  input  CMC,
  input  CLC,
  input  SETC,
  input  clock,
  input  Reset,
  output [63:0] DATAout
);

  wire or_1_out, xor_1_out;
  wire [63:0] multiplexer_1_out, pull_resistor_1_node, xor_2_out;

  or or_1 (or_1_out, CMC, CLC, SETC);
  xor xor_1 (xor_1_out, SETC, DATAin[0]);
  Pull_Resistor pull_resistor_1 (.node(pull_resistor_1_node));
  or or_2 (pull_resistor_1_node[0], CMC, xor_1_out);
  assign xor_2_out = pull_resistor_1_node ^ DATAin;  // XOR_Gate xor_2, 64 bits wide
  Multiplexer #(.width(64)) multiplexer_1 (.in0(DATAin), .in1(xor_2_out), .out(multiplexer_1_out), .sel(or_1_out));
  Pull_Resistor pull_resistor_2 (.node(multiplexer_1_out));
  Register #(.width(64)) RFLAGS (.D(multiplexer_1_out), .en(or_1_out), .clk(clock), .Q(DATAout), .clr(Reset));
endmodule

module block_memory_control (
  input  [63:0] in_1,
  input  [63:0] in_2,
  output [63:0] out_3,
  output [63:0] out_4
);
endmodule
